// Logisim project phone bill 4.0.circ as structural Verilog: 11 circuits, main circuit clock control
module clock_control (
  input  clock,
  output a,
  output b,
  output c,
  output d,
  output e,
  output f,
  output g,
  output a_2,
  output b_2,
  output c_2,
  output d_2,
  output e_2,
  output f_2,
  output g_2,
  output a_3,
  output b_3,
  output c_3,
  output d_3,
  output e_3,
  output f_3,
  output g_3,
  output a_4,
  output b_4,
  output c_4,
  output d_4,
  output e_4,
  output f_4,
  output g_4
);

  wire display_1_cout, display_2_cout, display_3_cout, mod_6_counter_1_x0, mod_6_counter_1_x1,
       mod_6_counter_1_x2, mod_6_counter_1_x3, mod_9_counter_1_x0, mod_9_counter_1_x1, mod_9_counter_1_x2,
       mod_9_counter_1_x3, mod_9_counter_2_x0, mod_9_counter_2_x1, mod_9_counter_2_x2, mod_9_counter_2_x3,
       mod_9_counter_3_x0, mod_9_counter_3_x1, mod_9_counter_3_x2, mod_9_counter_3_x3;

  mod_9_Counter mod_9_counter_1 (
    .clock(clock), .x3(mod_9_counter_1_x3), .x2(mod_9_counter_1_x2), .x1(mod_9_counter_1_x1),
    .x0(mod_9_counter_1_x0));
  mod_6_counter mod_6_counter_1 (
    .clock(display_1_cout), .x3(mod_6_counter_1_x3), .x2(mod_6_counter_1_x2), .x1(mod_6_counter_1_x1),
    .x0(mod_6_counter_1_x0));
  mod_9_Counter mod_9_counter_2 (
    .clock(display_2_cout), .x3(mod_9_counter_2_x3), .x2(mod_9_counter_2_x2), .x1(mod_9_counter_2_x1),
    .x0(mod_9_counter_2_x0));
  mod_9_Counter mod_9_counter_3 (
    .clock(display_3_cout), .x3(mod_9_counter_3_x3), .x2(mod_9_counter_3_x2), .x1(mod_9_counter_3_x1),
    .x0(mod_9_counter_3_x0));
  display display_1 (
    .x3(mod_9_counter_1_x3), .x2(mod_9_counter_1_x2), .x1(mod_9_counter_1_x1), .x0(mod_9_counter_1_x0),
    .a(a), .b(b), .c(c), .d(d), .e(e), .f(f), .g(g), .cout(display_1_cout));
  display display_2 (
    .x3(mod_6_counter_1_x3), .x2(mod_6_counter_1_x2), .x1(mod_6_counter_1_x1), .x0(mod_6_counter_1_x0),
    .a(a_2), .b(b_2), .c(c_2), .d(d_2), .e(e_2), .f(f_2), .g(g_2), .cout(display_2_cout));
  display display_3 (
    .x3(mod_9_counter_2_x3), .x2(mod_9_counter_2_x2), .x1(mod_9_counter_2_x1), .x0(mod_9_counter_2_x0),
    .a(a_3), .b(b_3), .c(c_3), .d(d_3), .e(e_3), .f(f_3), .g(g_3), .cout(display_3_cout));
  _4_bit_7_segment_display u_4_bit_7_segment_display_1 (
    .x3(mod_9_counter_3_x3), .x2(mod_9_counter_3_x2), .x1(mod_9_counter_3_x1), .a(a_4),
    .x0(mod_9_counter_3_x0), .b(b_4), .c(c_4), .d(d_4), .e(e_4), .f(f_4), .g(g_4));  // open: cout
endmodule

module _4_bit_7_segment_display (
  input  x3,
  input  x2,
  input  x1,
  input  x0,
  output a,
  output b,
  output c,
  output d,
  output e,
  output f,
  output g,
  output cout
);

  wire and_1_out, and_2_out, and_3_out, and_4_out, and_5_out, and_6_out, and_7_out, and_8_out, and_9_out,
       and_10_out, and_11_out, and_12_out, and_13_out, and_14_out, and_15_out, and_16_out, and_17_out,
       and_18_out, and_19_out, and_20_out, and_21_out, and_22_out, and_23_out, and_24_out, and_25_out,
       and_26_out, and_27_out, and_28_out, and_29_out, and_30_out, and_31_out, and_32_out, and_33_out,
       and_34_out, and_35_out, and_36_out, and_37_out, not_1_out, not_2_out, not_3_out, not_4_out, not_5_out,
       not_6_out, not_7_out, not_8_out, not_9_out, not_10_out, not_11_out, not_12_out, not_13_out,
       not_14_out, not_15_out, not_16_out, not_17_out, not_18_out, not_19_out, not_20_out, not_21_out,
       not_22_out, not_23_out, not_24_out, not_25_out, not_26_out, not_27_out, not_28_out, not_29_out,
       not_30_out, not_31_out, not_32_out, not_33_out, not_34_out, not_35_out, not_36_out, not_37_out,
       not_38_out, not_39_out, not_40_out, not_41_out, not_42_out, not_43_out, not_44_out, not_45_out,
       not_46_out, not_47_out, not_48_out, not_49_out;

  not not_1 (not_1_out, x2);
  and and_1 (and_1_out, not_1_out, not_2_out);
  not not_2 (not_2_out, x0);
  not not_3 (not_3_out, x3);
  and and_2 (and_2_out, not_3_out, x1);
  not not_4 (not_4_out, x3);
  and and_3 (and_3_out, not_4_out, x2, x0);
  and and_4 (and_4_out, x2, x1);
  not not_5 (not_5_out, x2);
  and and_5 (and_5_out, x3, not_5_out, not_6_out);
  not not_6 (not_6_out, x1);
  and and_6 (and_6_out, x3, not_7_out);
  not not_7 (not_7_out, x0);
  not not_8 (not_8_out, x3);
  and and_7 (and_7_out, not_8_out, not_9_out);
  not not_9 (not_9_out, x2);
  not not_10 (not_10_out, x3);
  not not_11 (not_11_out, x1);
  and and_8 (and_8_out, not_10_out, not_11_out, not_12_out);
  not not_12 (not_12_out, x0);
  not not_13 (not_13_out, x2);
  and and_9 (and_9_out, not_13_out, not_14_out);
  not not_14 (not_14_out, x0);
  not not_15 (not_15_out, x3);
  and and_10 (and_10_out, not_15_out, x1, x0);
  and and_11 (and_11_out, x3, not_16_out, x0);
  not not_16 (not_16_out, x1);
  not not_17 (not_17_out, x3);
  and and_12 (and_12_out, not_17_out, not_18_out);
  not not_18 (not_18_out, x1);
  not not_19 (not_19_out, x3);
  and and_13 (and_13_out, not_19_out, x0);
  not not_20 (not_20_out, x1);
  and and_14 (and_14_out, not_20_out, x0);
  not not_21 (not_21_out, x3);
  and and_15 (and_15_out, not_21_out, x2);
  and and_16 (and_16_out, x3, not_22_out);
  not not_22 (not_22_out, x2);
  not not_23 (not_23_out, x3);
  and and_17 (and_17_out, not_23_out, not_24_out, not_25_out);
  not not_24 (not_24_out, x2);
  not not_25 (not_25_out, x0);
  not not_26 (not_26_out, x2);
  and and_18 (and_18_out, not_26_out, x1, x0);
  and and_19 (and_19_out, x2, not_27_out, x0);
  not not_27 (not_27_out, x1);
  and and_20 (and_20_out, x2, x1, not_28_out);
  not not_28 (not_28_out, x0);
  and and_21 (and_21_out, x3, not_29_out);
  not not_29 (not_29_out, x1);
  not not_30 (not_30_out, x2);
  and and_22 (and_22_out, not_30_out, not_31_out);
  not not_31 (not_31_out, x0);
  and and_23 (and_23_out, x1, not_32_out);
  not not_32 (not_32_out, x0);
  and and_24 (and_24_out, x3, x1);
  and and_25 (and_25_out, x3, x2);
  not not_33 (not_33_out, x1);
  and and_26 (and_26_out, not_33_out, not_34_out);
  not not_34 (not_34_out, x0);
  not not_35 (not_35_out, x3);
  and and_27 (and_27_out, not_35_out, x2, not_36_out);
  not not_36 (not_36_out, x1);
  and and_28 (and_28_out, x2, not_37_out);
  not not_37 (not_37_out, x0);
  and and_29 (and_29_out, x3, not_38_out);
  not not_38 (not_38_out, x2);
  and and_30 (and_30_out, x3, x1);
  not not_39 (not_39_out, x2);
  and and_31 (and_31_out, not_39_out, x1);
  and and_32 (and_32_out, x1, not_40_out);
  not not_40 (not_40_out, x0);
  not not_41 (not_41_out, x3);
  and and_33 (and_33_out, not_41_out, x2, not_42_out);
  not not_42 (not_42_out, x1);
  and and_34 (and_34_out, x3, not_43_out);
  not not_43 (not_43_out, x2);
  and and_35 (and_35_out, x3, x0);
  not not_44 (not_44_out, x3);
  not not_45 (not_45_out, x2);
  not not_46 (not_46_out, x1);
  not not_47 (not_47_out, x0);
  not not_48 (not_48_out, x2);
  not not_49 (not_49_out, x1);
  or or_1 (b, and_7_out, and_8_out, and_9_out, and_10_out, and_11_out);
  or or_2 (c, and_12_out, and_13_out, and_14_out, and_15_out, and_16_out);
  or or_3 (d, and_17_out, and_18_out, and_19_out, and_20_out, and_21_out);
  or or_4 (e, and_22_out, and_23_out, and_24_out, and_25_out);
  or or_5 (f, and_26_out, and_27_out, and_28_out, and_29_out, and_30_out);
  or or_6 (g, and_31_out, and_32_out, and_33_out, and_34_out, and_35_out);
  and and_36 (and_36_out, not_44_out, not_45_out, not_46_out, not_47_out);
  or or_7 (cout, and_36_out, and_37_out);
  and and_37 (and_37_out, x3, not_48_out, not_49_out, x0);
  or or_8 (a, and_1_out, and_2_out, and_3_out, and_4_out, and_5_out, and_6_out);
endmodule

module timer (
  input  in_1
);

  wire bill_control_1_a, bill_control_1_a_2, bill_control_1_a_3, bill_control_1_a_4, bill_control_1_b,
       bill_control_1_b_2, bill_control_1_b_3, bill_control_1_b_4, bill_control_1_c, bill_control_1_c_2,
       bill_control_1_c_3, bill_control_1_c_4, bill_control_1_d, bill_control_1_d_2, bill_control_1_d_3,
       bill_control_1_d_4, bill_control_1_e, bill_control_1_e_2, bill_control_1_e_3, bill_control_1_e_4,
       bill_control_1_f, bill_control_1_f_2, bill_control_1_f_3, bill_control_1_f_4, bill_control_1_g,
       bill_control_1_g_2, bill_control_1_g_3, bill_control_1_g_4, clock_1_out, clock_control_1_a,
       clock_control_1_a_2, clock_control_1_a_3, clock_control_1_a_4, clock_control_1_b, clock_control_1_b_2,
       clock_control_1_b_3, clock_control_1_b_4, clock_control_1_c, clock_control_1_c_2, clock_control_1_c_3,
       clock_control_1_c_4, clock_control_1_d, clock_control_1_d_2, clock_control_1_d_3, clock_control_1_d_4,
       clock_control_1_e, clock_control_1_e_2, clock_control_1_e_3, clock_control_1_e_4, clock_control_1_f,
       clock_control_1_f_2, clock_control_1_f_3, clock_control_1_f_4, clock_control_1_g, clock_control_1_g_2,
       clock_control_1_g_3, clock_control_1_g_4;

  Clock clock_1 (.out(clock_1_out));
  bill_control bill_control_1 (
    .clock(clock_1_out), .a(bill_control_1_a), .b(bill_control_1_b), .c(bill_control_1_c),
    .d(bill_control_1_d), .e(bill_control_1_e), .f(bill_control_1_f), .g(bill_control_1_g),
    .a_2(bill_control_1_a_2), .b_2(bill_control_1_b_2), .c_2(bill_control_1_c_2), .d_2(bill_control_1_d_2),
    .e_2(bill_control_1_e_2), .f_2(bill_control_1_f_2), .g_2(bill_control_1_g_2), .a_3(bill_control_1_a_3),
    .b_3(bill_control_1_b_3), .c_3(bill_control_1_c_3), .d_3(bill_control_1_d_3), .e_3(bill_control_1_e_3),
    .f_3(bill_control_1_f_3), .g_3(bill_control_1_g_3), .a_4(bill_control_1_a_4), .b_4(bill_control_1_b_4),
    .c_4(bill_control_1_c_4), .d_4(bill_control_1_d_4), .e_4(bill_control_1_e_4), .f_4(bill_control_1_f_4),
    .g_4(bill_control_1_g_4));
  clock_control clock_control_1 (
    .a_2(clock_control_1_a_2), .b_2(clock_control_1_b_2), .c_2(clock_control_1_c_2),
    .d_2(clock_control_1_d_2), .e_2(clock_control_1_e_2), .f_2(clock_control_1_f_2),
    .g_2(clock_control_1_g_2), .a_3(clock_control_1_a_3), .b_3(clock_control_1_b_3),
    .e_3(clock_control_1_e_3), .f_3(clock_control_1_f_3), .g_3(clock_control_1_g_3),
    .d_3(clock_control_1_d_3), .c_3(clock_control_1_c_3), .clock(clock_1_out), .a_4(clock_control_1_a_4),
    .b_4(clock_control_1_b_4), .c_4(clock_control_1_c_4), .d_4(clock_control_1_d_4),
    .e_4(clock_control_1_e_4), .f_4(clock_control_1_f_4), .g_4(clock_control_1_g_4), .a(clock_control_1_a),
    .b(clock_control_1_b), .c(clock_control_1_c), .d(clock_control_1_d), .e(clock_control_1_e),
    .f(clock_control_1_f), .g(clock_control_1_g));
  _7_Segment_Display u_7_segment_display_1 (
    .g(clock_control_1_g_4), .f(clock_control_1_f_4), .a(clock_control_1_a_4), .b(clock_control_1_b_4),
    .e(clock_control_1_e_4), .d(clock_control_1_d_4), .c(clock_control_1_c_4));  // open: dp
  _7_Segment_Display u_7_segment_display_2 (
    .g(clock_control_1_g_2), .f(clock_control_1_f_2), .a(clock_control_1_a_2), .b(clock_control_1_b_2),
    .e(clock_control_1_e_2), .d(clock_control_1_d_2), .c(clock_control_1_c_2));  // open: dp
  _7_Segment_Display u_7_segment_display_3 (
    .g(clock_control_1_g_3), .f(clock_control_1_f_3), .a(clock_control_1_a_3), .b(clock_control_1_b_3),
    .e(clock_control_1_e_3), .d(clock_control_1_d_3), .c(clock_control_1_c_3));  // open: dp
  _7_Segment_Display u_7_segment_display_4 (
    .g(clock_control_1_g), .f(clock_control_1_f), .a(clock_control_1_a), .b(clock_control_1_b),
    .e(clock_control_1_e), .d(clock_control_1_d), .c(clock_control_1_c));  // open: dp
  _7_Segment_Display u_7_segment_display_5 (
    .g(bill_control_1_g_4), .f(bill_control_1_f_4), .a(bill_control_1_a_4), .b(bill_control_1_b_4),
    .e(bill_control_1_e_4), .d(bill_control_1_d_4), .c(bill_control_1_c_4));  // open: dp
  _7_Segment_Display u_7_segment_display_6 (
    .g(bill_control_1_g_3), .f(bill_control_1_f_3), .a(bill_control_1_a_3), .b(bill_control_1_b_3),
    .e(bill_control_1_e_3), .d(bill_control_1_d_3), .c(bill_control_1_c_3));  // open: dp
  _7_Segment_Display u_7_segment_display_7 (
    .g(bill_control_1_g_2), .f(bill_control_1_f_2), .a(bill_control_1_a_2), .b(bill_control_1_b_2),
    .e(bill_control_1_e_2), .d(bill_control_1_d_2), .c(bill_control_1_c_2));  // open: dp
  _7_Segment_Display u_7_segment_display_8 (
    .g(bill_control_1_g), .f(bill_control_1_f), .a(bill_control_1_a), .b(bill_control_1_b),
    .e(bill_control_1_e), .d(bill_control_1_d), .c(bill_control_1_c));  // open: dp
endmodule

module display (
  input  x3,
  input  x2,
  input  x1,
  input  x0,
  output a,
  output b,
  output c,
  output d,
  output e,
  output f,
  output g,
  output cout
);

  wire and_1_out, and_2_out, and_3_out, and_4_out, and_5_out, and_6_out, and_7_out, and_8_out, and_9_out,
       and_10_out, and_11_out, and_12_out, and_13_out, and_14_out, and_15_out, and_16_out, and_17_out,
       and_18_out, and_19_out, and_20_out, and_21_out, and_22_out, and_23_out, and_24_out, and_25_out,
       and_26_out, and_27_out, and_28_out, and_29_out, and_30_out, and_31_out, and_32_out, and_33_out,
       and_34_out, and_35_out, and_36_out, and_37_out, not_1_out, not_2_out, not_3_out, not_4_out, not_5_out,
       not_6_out, not_7_out, not_8_out, not_9_out, not_10_out, not_11_out, not_12_out, not_13_out,
       not_14_out, not_15_out, not_16_out, not_17_out, not_18_out, not_19_out, not_20_out, not_21_out,
       not_22_out, not_23_out, not_24_out, not_25_out, not_26_out, not_27_out, not_28_out, not_29_out,
       not_30_out, not_31_out, not_32_out, not_33_out, not_34_out, not_35_out, not_36_out, not_37_out,
       not_38_out, not_39_out, not_40_out, not_41_out, not_42_out, not_43_out, not_44_out, not_45_out,
       not_46_out, not_47_out, not_48_out, not_49_out;

  not not_1 (not_1_out, x2);
  and and_1 (and_1_out, not_1_out, not_2_out);
  not not_2 (not_2_out, x0);
  not not_3 (not_3_out, x3);
  and and_2 (and_2_out, not_3_out, x1);
  not not_4 (not_4_out, x3);
  and and_3 (and_3_out, not_4_out, x2, x0);
  and and_4 (and_4_out, x2, x1);
  and and_5 (and_5_out, x3, not_5_out, not_6_out);
  not not_5 (not_5_out, x2);
  not not_6 (not_6_out, x1);
  and and_6 (and_6_out, x3, not_7_out);
  not not_7 (not_7_out, x0);
  not not_8 (not_8_out, x3);
  and and_7 (and_7_out, not_8_out, not_9_out);
  not not_9 (not_9_out, x2);
  not not_10 (not_10_out, x3);
  and and_8 (and_8_out, not_10_out, not_11_out, not_12_out);
  not not_11 (not_11_out, x1);
  not not_12 (not_12_out, x0);
  not not_13 (not_13_out, x2);
  and and_9 (and_9_out, not_13_out, not_14_out);
  not not_14 (not_14_out, x0);
  not not_15 (not_15_out, x3);
  and and_10 (and_10_out, not_15_out, x1, x0);
  not not_16 (not_16_out, x1);
  and and_11 (and_11_out, x3, not_16_out, x0);
  not not_17 (not_17_out, x3);
  and and_12 (and_12_out, not_17_out, not_18_out);
  not not_18 (not_18_out, x1);
  not not_19 (not_19_out, x3);
  and and_13 (and_13_out, not_19_out, x0);
  not not_20 (not_20_out, x1);
  and and_14 (and_14_out, not_20_out, x0);
  not not_21 (not_21_out, x3);
  and and_15 (and_15_out, not_21_out, x2);
  and and_16 (and_16_out, x3, not_22_out);
  not not_22 (not_22_out, x2);
  not not_23 (not_23_out, x3);
  and and_17 (and_17_out, not_23_out, not_24_out, not_25_out);
  not not_24 (not_24_out, x2);
  not not_25 (not_25_out, x0);
  not not_26 (not_26_out, x2);
  and and_18 (and_18_out, not_26_out, x1, x0);
  and and_19 (and_19_out, x2, not_27_out, x0);
  not not_27 (not_27_out, x1);
  and and_20 (and_20_out, x2, x1, not_28_out);
  not not_28 (not_28_out, x0);
  and and_21 (and_21_out, x3, not_29_out);
  not not_29 (not_29_out, x1);
  not not_30 (not_30_out, x2);
  and and_22 (and_22_out, not_30_out, not_31_out);
  not not_31 (not_31_out, x0);
  and and_23 (and_23_out, x1, not_32_out);
  not not_32 (not_32_out, x0);
  and and_24 (and_24_out, x3, x1);
  and and_25 (and_25_out, x3, x2);
  not not_33 (not_33_out, x1);
  and and_26 (and_26_out, not_33_out, not_34_out);
  not not_34 (not_34_out, x0);
  not not_35 (not_35_out, x3);
  and and_27 (and_27_out, not_35_out, x2, not_36_out);
  not not_36 (not_36_out, x1);
  and and_28 (and_28_out, x2, not_37_out);
  not not_37 (not_37_out, x0);
  and and_29 (and_29_out, x3, not_38_out);
  not not_38 (not_38_out, x2);
  and and_30 (and_30_out, x3, x1);
  not not_39 (not_39_out, x2);
  and and_31 (and_31_out, not_39_out, x1);
  and and_32 (and_32_out, x1, not_40_out);
  not not_40 (not_40_out, x0);
  not not_41 (not_41_out, x3);
  and and_33 (and_33_out, not_41_out, x2, not_42_out);
  not not_42 (not_42_out, x1);
  and and_34 (and_34_out, x3, not_43_out);
  not not_43 (not_43_out, x2);
  and and_35 (and_35_out, x3, x0);
  not not_44 (not_44_out, x3);
  not not_45 (not_45_out, x2);
  not not_46 (not_46_out, x1);
  not not_47 (not_47_out, x0);
  not not_48 (not_48_out, x2);
  not not_49 (not_49_out, x0);
  or or_1 (b, and_7_out, and_8_out, and_9_out, and_10_out, and_11_out);
  or or_2 (c, and_12_out, and_13_out, and_14_out, and_15_out, and_16_out);
  or or_3 (d, and_17_out, and_18_out, and_19_out, and_20_out, and_21_out);
  or or_4 (e, and_22_out, and_23_out, and_24_out, and_25_out);
  or or_5 (f, and_26_out, and_27_out, and_28_out, and_29_out, and_30_out);
  or or_6 (g, and_31_out, and_32_out, and_33_out, and_34_out, and_35_out);
  and and_36 (and_36_out, not_44_out, not_45_out, not_46_out, not_47_out);
  or or_7 (cout, and_36_out, and_37_out);
  and and_37 (and_37_out, x3, not_48_out, x1, not_49_out);
  or or_8 (a, and_1_out, and_2_out, and_3_out, and_4_out, and_5_out, and_6_out);
endmodule

module mod_9_Counter (
  input  clock,
  output x3,
  output x2,
  output x1,
  output x0
);

  wire and_1_out, and_2_out, and_3_out, and_4_out, and_5_out, and_6_out, and_7_out, not_1_out, not_2_out,
       not_3_out, not_4_out, not_5_out, not_6_out, not_7_out, not_8_out, or_1_out, or_2_out, or_3_out;

  not not_1 (not_1_out, x0);
  not not_2 (not_2_out, x0);
  not not_3 (not_3_out, x2);
  not not_4 (not_4_out, x1);
  not not_5 (not_5_out, x0);
  not not_6 (not_6_out, x3);
  not not_7 (not_7_out, x1);
  not not_8 (not_8_out, x0);
  and and_1 (and_1_out, x2, x1, x0);
  and and_2 (and_2_out, x3, not_2_out);
  and and_3 (and_3_out, not_3_out, x1, x0);
  and and_4 (and_4_out, x2, not_4_out);
  and and_5 (and_5_out, x2, not_5_out);
  and and_6 (and_6_out, not_6_out, not_7_out, x0);
  and and_7 (and_7_out, x1, not_8_out);
  or or_1 (or_1_out, and_1_out, and_2_out);
  or or_2 (or_2_out, and_3_out, and_4_out, and_5_out);
  or or_3 (or_3_out, and_6_out, and_7_out);
  D_Flip_Flop d_ff_1 (.clk(clock), .D(or_1_out), .Q(x3));  // open: Qn, preset, en, reset
  D_Flip_Flop d_ff_2 (.clk(clock), .D(or_2_out), .Q(x2));  // open: Qn, preset, en, reset
  D_Flip_Flop d_ff_3 (.clk(clock), .D(or_3_out), .Q(x1));  // open: Qn, preset, en, reset
  D_Flip_Flop d_ff_4 (.clk(clock), .D(not_1_out), .Q(x0));  // open: Qn, preset, en, reset
endmodule

module mod_6_counter (
  input  clock,
  output x3,
  output x2,
  output x1,
  output x0
);

  wire and_1_out, and_2_out, and_3_out, and_4_out, not_1_out, not_2_out, not_3_out, not_4_out, not_5_out,
       or_1_out, or_2_out;

  not not_1 (not_1_out, x0);
  not not_2 (not_2_out, x2);
  not not_3 (not_3_out, x1);
  not not_4 (not_4_out, x0);
  not not_5 (not_5_out, x0);
  and and_1 (and_1_out, x1, x0);
  and and_2 (and_2_out, x2, not_1_out);
  and and_3 (and_3_out, not_2_out, not_3_out, x0);
  and and_4 (and_4_out, x1, not_4_out);
  or or_1 (or_1_out, and_1_out, and_2_out);
  or or_2 (or_2_out, and_3_out, and_4_out);
  D_Flip_Flop d_ff_1 (.clk(clock), .D(1'b0), .Q(x3));  // open: Qn, preset, en, reset
  D_Flip_Flop d_ff_2 (.clk(clock), .D(or_1_out), .Q(x2));  // open: Qn, preset, en, reset
  D_Flip_Flop d_ff_3 (.clk(clock), .D(or_2_out), .Q(x1));  // open: Qn, preset, en, reset
  D_Flip_Flop d_ff_4 (.clk(clock), .D(not_5_out), .Q(x0));  // open: Qn, preset, en, reset
endmodule

module _2_sec (
  input  clock,
  output x3,
  output x2,
  output x1,
  output x0
);

  wire not_1_out;

  not not_1 (not_1_out, x0);
  D_Flip_Flop d_ff_1 (.clk(clock), .D(1'b0), .Q(x3));  // open: Qn, preset, en, reset
  D_Flip_Flop d_ff_2 (.clk(clock), .D(1'b0), .Q(x2));  // open: Qn, preset, en, reset
  D_Flip_Flop d_ff_3 (.clk(clock), .D(1'b0), .Q(x1));  // open: Qn, preset, en, reset
  D_Flip_Flop d_ff_4 (.clk(clock), .D(not_1_out), .Q(x0));  // open: Qn, preset, en, reset
endmodule

module sample (
  input  x3,
  input  x2,
  input  x1,
  input  x0,
  output a,
  output b,
  output c,
  output d
);

  wire and_1_out, and_2_out, and_3_out, and_4_out, and_5_out, and_6_out, and_7_out, not_1_out, not_2_out,
       not_3_out, not_4_out, not_5_out, not_6_out, not_7_out;

  not not_1 (not_1_out, x0);
  not not_2 (not_2_out, x2);
  not not_3 (not_3_out, x1);
  not not_4 (not_4_out, x0);
  not not_5 (not_5_out, x3);
  not not_6 (not_6_out, x1);
  not not_7 (not_7_out, x0);
  not not_8 (d, x0);
  and and_1 (and_1_out, x2, x1, x0);
  and and_2 (and_2_out, x3, not_1_out);
  and and_3 (and_3_out, not_2_out, x1, x0);
  and and_4 (and_4_out, x2, not_3_out);
  and and_5 (and_5_out, x2, not_4_out);
  and and_6 (and_6_out, not_5_out, not_6_out, x0);
  and and_7 (and_7_out, x1, not_7_out);
  or or_1 (a, and_1_out, and_2_out);
  or or_2 (b, and_3_out, and_4_out, and_5_out);
  or or_3 (c, and_6_out, and_7_out);
endmodule

module bill_control (
  input  clock,
  output a,
  output b,
  output c,
  output d,
  output e,
  output f,
  output g,
  output a_2,
  output b_2,
  output c_2,
  output d_2,
  output e_2,
  output f_2,
  output g_2,
  output a_3,
  output b_3,
  output c_3,
  output d_3,
  output e_3,
  output f_3,
  output g_3,
  output a_4,
  output b_4,
  output c_4,
  output d_4,
  output e_4,
  output f_4,
  output g_4
);

  wire display_1_cout, display_2_cout, display_3_cout, display_4_cout, mod_9_counter_1_x0,
       mod_9_counter_1_x1, mod_9_counter_1_x2, mod_9_counter_1_x3, mod_9_counter_2_x0, mod_9_counter_2_x1,
       mod_9_counter_2_x2, mod_9_counter_2_x3, mod_9_counter_3_x0, mod_9_counter_3_x1, mod_9_counter_3_x2,
       mod_9_counter_3_x3, mod_9_counter_4_x0, mod_9_counter_4_x1, mod_9_counter_4_x2, mod_9_counter_4_x3,
       n2_sec_1_x0, n2_sec_1_x1, n2_sec_1_x2, n2_sec_1_x3;

  _2_sec u_2_sec_1 (.clock(clock), .x3(n2_sec_1_x3), .x2(n2_sec_1_x2), .x1(n2_sec_1_x1), .x0(n2_sec_1_x0));
  display display_1 (
    .x3(n2_sec_1_x3), .x2(n2_sec_1_x2), .x1(n2_sec_1_x1), .x0(n2_sec_1_x0), .cout(display_1_cout));  // open: a, b, c, d, e, f, g
  mod_9_Counter mod_9_counter_1 (
    .clock(display_1_cout), .x3(mod_9_counter_1_x3), .x2(mod_9_counter_1_x2), .x1(mod_9_counter_1_x1),
    .x0(mod_9_counter_1_x0));
  mod_9_Counter mod_9_counter_2 (
    .clock(display_2_cout), .x3(mod_9_counter_2_x3), .x2(mod_9_counter_2_x2), .x1(mod_9_counter_2_x1),
    .x0(mod_9_counter_2_x0));
  mod_9_Counter mod_9_counter_3 (
    .clock(display_3_cout), .x3(mod_9_counter_3_x3), .x2(mod_9_counter_3_x2), .x1(mod_9_counter_3_x1),
    .x0(mod_9_counter_3_x0));
  mod_9_Counter mod_9_counter_4 (
    .clock(display_4_cout), .x3(mod_9_counter_4_x3), .x2(mod_9_counter_4_x2), .x1(mod_9_counter_4_x1),
    .x0(mod_9_counter_4_x0));
  display display_2 (
    .x3(mod_9_counter_1_x3), .x2(mod_9_counter_1_x2), .x1(mod_9_counter_1_x1), .x0(mod_9_counter_1_x0),
    .a(a), .b(b), .c(c), .d(d), .e(e), .f(f), .g(g), .cout(display_2_cout));
  display display_3 (
    .x3(mod_9_counter_2_x3), .x2(mod_9_counter_2_x2), .x1(mod_9_counter_2_x1), .x0(mod_9_counter_2_x0),
    .a(a_2), .b(b_2), .c(c_2), .d(d_2), .e(e_2), .f(f_2), .g(g_2), .cout(display_3_cout));
  display display_4 (
    .x3(mod_9_counter_3_x3), .x2(mod_9_counter_3_x2), .x1(mod_9_counter_3_x1), .x0(mod_9_counter_3_x0),
    .a(a_3), .b(b_3), .c(c_3), .d(d_3), .e(e_3), .f(f_3), .g(g_3), .cout(display_4_cout));
  display display_5 (
    .x3(mod_9_counter_4_x3), .x2(mod_9_counter_4_x2), .x1(mod_9_counter_4_x1), .x0(mod_9_counter_4_x0),
    .a(a_4), .b(b_4), .c(c_4), .d(d_4), .e(e_4), .f(f_4), .g(g_4));  // open: cout
endmodule

module main_display (
  output a,
  output b,
  output c,
  output d,
  output e,
  output f,
  output g,
  output c_2,
  output d_2,
  output a_2,
  output e_2,
  output b_2,
  output f_2,
  output g_2,
  output a_3,
  output b_3,
  output c_3,
  output d_3,
  output e_3,
  output a_4,
  output f_3,
  output b_4,
  output g_3,
  output c_4,
  output d_4,
  output e_4,
  output f_4,
  output g_4,
  output a_5,
  output b_5,
  output c_5,
  output d_5,
  output e_5,
  output f_5,
  output g_5,
  output a_6,
  output b_6,
  output c_6,
  output d_6,
  output e_6,
  output f_6,
  output g_6,
  output a_7,
  output b_7,
  output c_7,
  output d_7,
  output e_7,
  output f_7,
  output g_7,
  output a_8,
  output b_8,
  output c_8,
  output d_8,
  output e_8,
  output f_8,
  output g_8
);

  wire clock_out;

  Clock clock (.out(clock_out));
  clock_control clock_control_1 (
    .a_2(a_2), .b_2(b_2), .c_2(c_2), .d_2(d_2), .e_2(e_2), .f_2(f_2), .g_2(g_2), .a_3(a_3), .b_3(b_3),
    .e_3(e_3), .f_3(f_3), .g_3(g_3), .d_3(d_3), .c_3(c_3), .clock(clock_out), .a_4(a_4), .b_4(b_4),
    .c_4(c_4), .d_4(d_4), .e_4(e_4), .f_4(f_4), .g_4(g_4), .a(a), .b(b), .c(c), .d(d), .e(e), .f(f), .g(g));
  bill_control bill_control_1 (
    .clock(clock_out), .a(a_5), .b(b_5), .c(c_5), .d(d_5), .e(e_5), .f(f_5), .g(g_5), .a_2(a_6), .b_2(b_6),
    .c_2(c_6), .d_2(d_6), .e_2(e_6), .f_2(f_6), .g_2(g_6), .a_3(a_7), .b_3(b_7), .c_3(c_7), .d_3(d_7),
    .e_3(e_7), .f_3(f_7), .g_3(g_7), .a_4(a_8), .b_4(b_8), .c_4(c_8), .d_4(d_8), .e_4(e_8), .f_4(f_8),
    .g_4(g_8));
endmodule

module telephone_billing_system (
);

  wire main_display_1_a, main_display_1_a_2, main_display_1_a_3, main_display_1_a_4, main_display_1_a_5,
       main_display_1_a_6, main_display_1_a_7, main_display_1_a_8, main_display_1_b, main_display_1_b_2,
       main_display_1_b_3, main_display_1_b_4, main_display_1_b_5, main_display_1_b_6, main_display_1_b_7,
       main_display_1_b_8, main_display_1_c, main_display_1_c_2, main_display_1_c_3, main_display_1_c_4,
       main_display_1_c_5, main_display_1_c_6, main_display_1_c_7, main_display_1_c_8, main_display_1_d,
       main_display_1_d_2, main_display_1_d_3, main_display_1_d_4, main_display_1_d_5, main_display_1_d_6,
       main_display_1_d_7, main_display_1_d_8, main_display_1_e, main_display_1_e_2, main_display_1_e_3,
       main_display_1_e_4, main_display_1_e_5, main_display_1_e_6, main_display_1_e_7, main_display_1_e_8,
       main_display_1_f, main_display_1_f_2, main_display_1_f_3, main_display_1_f_4, main_display_1_f_5,
       main_display_1_f_6, main_display_1_f_7, main_display_1_f_8, main_display_1_g, main_display_1_g_2,
       main_display_1_g_3, main_display_1_g_4, main_display_1_g_5, main_display_1_g_6, main_display_1_g_7,
       main_display_1_g_8;

  _7_Segment_Display u_7_segment_display_1 (
    .g(main_display_1_g_4), .f(main_display_1_f_4), .a(main_display_1_a_4), .b(main_display_1_b_4),
    .e(main_display_1_e_4), .d(main_display_1_d_4), .c(main_display_1_c_4));  // open: dp
  _7_Segment_Display u_7_segment_display_2 (
    .g(main_display_1_g_3), .f(main_display_1_f_3), .a(main_display_1_a_3), .b(main_display_1_b_3),
    .e(main_display_1_e_3), .d(main_display_1_d_3), .c(main_display_1_c_3));  // open: dp
  _7_Segment_Display u_7_segment_display_3 (
    .g(main_display_1_g), .f(main_display_1_f), .a(main_display_1_a), .b(main_display_1_b),
    .e(main_display_1_e), .d(main_display_1_d), .c(main_display_1_c));  // open: dp
  _7_Segment_Display u_7_segment_display_4 (
    .g(main_display_1_g_2), .f(main_display_1_f_2), .a(main_display_1_a_2), .b(main_display_1_b_2),
    .e(main_display_1_e_2), .d(main_display_1_d_2), .c(main_display_1_c_2));  // open: dp
  main_display main_display_1 (
    .a(main_display_1_a), .b(main_display_1_b), .c(main_display_1_c), .d(main_display_1_d),
    .e(main_display_1_e), .f(main_display_1_f), .g(main_display_1_g), .c_2(main_display_1_c_2),
    .d_2(main_display_1_d_2), .a_2(main_display_1_a_2), .e_2(main_display_1_e_2), .b_2(main_display_1_b_2),
    .f_2(main_display_1_f_2), .g_2(main_display_1_g_2), .a_3(main_display_1_a_3), .b_3(main_display_1_b_3),
    .c_3(main_display_1_c_3), .d_3(main_display_1_d_3), .e_3(main_display_1_e_3), .a_4(main_display_1_a_4),
    .f_3(main_display_1_f_3), .b_4(main_display_1_b_4), .g_3(main_display_1_g_3), .c_4(main_display_1_c_4),
    .d_4(main_display_1_d_4), .e_4(main_display_1_e_4), .f_4(main_display_1_f_4), .g_4(main_display_1_g_4),
    .a_5(main_display_1_a_5), .b_5(main_display_1_b_5), .c_5(main_display_1_c_5), .d_5(main_display_1_d_5),
    .e_5(main_display_1_e_5), .f_5(main_display_1_f_5), .g_5(main_display_1_g_5), .a_6(main_display_1_a_6),
    .b_6(main_display_1_b_6), .c_6(main_display_1_c_6), .d_6(main_display_1_d_6), .e_6(main_display_1_e_6),
    .f_6(main_display_1_f_6), .g_6(main_display_1_g_6), .a_7(main_display_1_a_7), .b_7(main_display_1_b_7),
    .c_7(main_display_1_c_7), .d_7(main_display_1_d_7), .e_7(main_display_1_e_7), .f_7(main_display_1_f_7),
    .g_7(main_display_1_g_7), .a_8(main_display_1_a_8), .b_8(main_display_1_b_8), .c_8(main_display_1_c_8),
    .d_8(main_display_1_d_8), .e_8(main_display_1_e_8), .f_8(main_display_1_f_8), .g_8(main_display_1_g_8));
  _7_Segment_Display u_7_segment_display_5 (
    .g(main_display_1_g_8), .f(main_display_1_f_8), .a(main_display_1_a_8), .b(main_display_1_b_8),
    .e(main_display_1_e_8), .d(main_display_1_d_8), .c(main_display_1_c_8));  // open: dp
  _7_Segment_Display u_7_segment_display_6 (
    .g(main_display_1_g_7), .f(main_display_1_f_7), .a(main_display_1_a_7), .b(main_display_1_b_7),
    .e(main_display_1_e_7), .d(main_display_1_d_7), .c(main_display_1_c_7));  // open: dp
  _7_Segment_Display u_7_segment_display_7 (
    .g(main_display_1_g_6), .f(main_display_1_f_6), .a(main_display_1_a_6), .b(main_display_1_b_6),
    .e(main_display_1_e_6), .d(main_display_1_d_6), .c(main_display_1_c_6));  // open: dp
  _7_Segment_Display u_7_segment_display_8 (
    .g(main_display_1_g_5), .f(main_display_1_f_5), .a(main_display_1_a_5), .b(main_display_1_b_5),
    .e(main_display_1_e_5), .d(main_display_1_d_5), .c(main_display_1_c_5));  // open: dp
endmodule
