// Logisim project 9 COUNTER.circ as structural Verilog: 18 circuits, main circuit bcd2_7seg_disp
module bcd2_7seg_disp (
  input  X3,
  input  X2,
  input  X1,
  input  X0,
  output a,
  output b,
  output c,
  output d,
  output e,
  output f,
  output g
);

  wire and_1_out, and_2_out, and_3_out, and_4_out, and_5_out, and_6_out, and_7_out, and_8_out, and_9_out,
       and_10_out, and_11_out, and_12_out, and_13_out, and_14_out, and_15_out, and_16_out, and_17_out,
       and_18_out, and_19_out, and_20_out, and_21_out, and_22_out, and_23_out, and_24_out, and_25_out,
       and_26_out, and_27_out, and_28_out, and_29_out, and_30_out, and_31_out, and_32_out, and_33_out,
       not_1_out, not_2_out, not_3_out, not_4_out, not_5_out, not_6_out, not_7_out, not_8_out, not_9_out,
       not_10_out, not_11_out, not_12_out, not_13_out, not_14_out, not_15_out, not_16_out, not_17_out,
       not_18_out, not_19_out, not_20_out, not_21_out, not_22_out, not_23_out, not_24_out, not_25_out,
       not_26_out, not_27_out, not_28_out, not_29_out, not_30_out, not_31_out, not_32_out, not_33_out,
       not_34_out, not_35_out, not_36_out, not_37_out, not_38_out, not_39_out, not_40_out, not_41_out;

  not not_1 (not_1_out, X2);
  and and_1 (and_1_out, not_1_out, not_2_out);
  not not_2 (not_2_out, X0);
  not not_3 (not_3_out, X3);
  and and_2 (and_2_out, not_3_out, X1);
  not not_4 (not_4_out, X3);
  and and_3 (and_3_out, not_4_out, X2, X0);
  and and_4 (and_4_out, X2, X1);
  and and_5 (and_5_out, X3, not_5_out, not_6_out);
  not not_5 (not_5_out, X2);
  not not_6 (not_6_out, X1);
  and and_6 (and_6_out, X3, not_7_out);
  not not_7 (not_7_out, X0);
  not not_8 (not_8_out, X3);
  and and_7 (and_7_out, not_8_out, not_9_out);
  not not_9 (not_9_out, X2);
  not not_10 (not_10_out, X3);
  not not_11 (not_11_out, X1);
  and and_8 (and_8_out, not_10_out, not_11_out, not_12_out);
  not not_12 (not_12_out, X0);
  not not_13 (not_13_out, X2);
  and and_9 (and_9_out, not_13_out, not_14_out);
  not not_14 (not_14_out, X0);
  not not_15 (not_15_out, X3);
  and and_10 (and_10_out, not_15_out, X1, X0);
  and and_11 (and_11_out, X3, not_16_out, X0);
  not not_16 (not_16_out, X1);
  not not_17 (not_17_out, X3);
  and and_12 (and_12_out, not_17_out, not_18_out);
  not not_18 (not_18_out, X1);
  not not_19 (not_19_out, X3);
  and and_13 (and_13_out, not_19_out, X0);
  not not_20 (not_20_out, X1);
  and and_14 (and_14_out, not_20_out, X0);
  not not_21 (not_21_out, X3);
  and and_15 (and_15_out, not_21_out, X2);
  and and_16 (and_16_out, X3, not_22_out);
  not not_22 (not_22_out, X2);
  not not_23 (not_23_out, X3);
  not not_24 (not_24_out, X2);
  and and_17 (and_17_out, not_23_out, not_24_out, not_25_out);
  not not_25 (not_25_out, X0);
  not not_26 (not_26_out, X2);
  and and_18 (and_18_out, not_26_out, X1, X0);
  and and_19 (and_19_out, X2, not_27_out, X0);
  not not_27 (not_27_out, X1);
  and and_20 (and_20_out, X2, X1, not_28_out);
  not not_28 (not_28_out, X0);
  and and_21 (and_21_out, X3, not_29_out);
  not not_29 (not_29_out, X1);
  not not_30 (not_30_out, X2);
  and and_22 (and_22_out, not_30_out, not_31_out);
  not not_31 (not_31_out, X0);
  and and_23 (and_23_out, X1, not_32_out);
  not not_32 (not_32_out, X0);
  and and_24 (and_24_out, X3, X1);
  and and_25 (and_25_out, X3, X2);
  not not_33 (not_33_out, X1);
  and and_26 (and_26_out, not_33_out, not_34_out);
  not not_34 (not_34_out, X0);
  not not_35 (not_35_out, X3);
  and and_27 (and_27_out, not_35_out, X2, not_36_out);
  not not_36 (not_36_out, X1);
  and and_28 (and_28_out, X2, not_37_out);
  not not_37 (not_37_out, X0);
  and and_29 (and_29_out, X3, not_38_out);
  not not_38 (not_38_out, X2);
  and and_30 (and_30_out, X3, X1);
  not not_39 (not_39_out, X2);
  and and_31 (and_31_out, not_39_out, X1);
  and and_32 (and_32_out, X1, not_40_out);
  not not_40 (not_40_out, X0);
  and and_33 (and_33_out, X2, not_41_out);
  not not_41 (not_41_out, X1);
  or or_1 (b, and_7_out, and_8_out, and_9_out, and_10_out, and_11_out);
  or or_2 (c, and_12_out, and_13_out, and_14_out, and_15_out, and_16_out);
  or or_3 (d, and_17_out, and_18_out, and_19_out, and_20_out, and_21_out);
  or or_4 (e, and_22_out, and_23_out, and_24_out, and_25_out);
  or or_5 (f, and_26_out, and_27_out, and_28_out, and_29_out, and_30_out);
  or or_6 (g, and_31_out, and_32_out, and_33_out, X3);
  or or_7 (a, and_1_out, and_2_out, and_3_out, and_4_out, and_5_out, and_6_out);
  _7_Segment_Display u_7_segment_display_1 (.g(g), .f(f), .a(a), .b(b), .e(e), .d(d), .c(c));  // open: dp
endmodule

// x0
module asynchronous_counter (
  input  in_1,
  input  in_2,
  input  in_3,
  output x1,
  output x0,
  output x2
);

  wire bcd2_7seg_disp_1_a, bcd2_7seg_disp_1_b, bcd2_7seg_disp_1_c, bcd2_7seg_disp_1_d, bcd2_7seg_disp_1_e,
       bcd2_7seg_disp_1_f, bcd2_7seg_disp_1_g, clock_1_out, xor_1_out, xor_2_out;

  Clock clock_1 (.out(clock_1_out));
  J_K_Flip_Flop #(.trigger("falling")) j_k_ff_1 (
    .J(1'b1), .clk(clock_1_out), .K(1'b1), .Q(x0));  // open: Qn, preset, en, reset
  xor xor_1 (xor_1_out, x0, 1'b1);
  J_K_Flip_Flop #(.trigger("falling")) j_k_ff_2 (
    .J(1'b1), .clk(xor_1_out), .K(1'b1), .Q(x1));  // open: Qn, preset, en, reset
  xor xor_2 (xor_2_out, x1, 1'b1);
  bcd2_7seg_disp bcd2_7seg_disp_1 (
    .X3(in_3), .X2(x2), .X1(x1), .X0(x0), .a(bcd2_7seg_disp_1_a), .b(bcd2_7seg_disp_1_b),
    .c(bcd2_7seg_disp_1_c), .d(bcd2_7seg_disp_1_d), .e(bcd2_7seg_disp_1_e), .f(bcd2_7seg_disp_1_f),
    .g(bcd2_7seg_disp_1_g));
  J_K_Flip_Flop #(.trigger("falling")) j_k_ff_3 (
    .J(1'b1), .clk(xor_2_out), .K(1'b1), .Q(x2));  // open: Qn, preset, en, reset
  _7_Segment_Display u_7_segment_display_1 (
    .g(bcd2_7seg_disp_1_g), .f(bcd2_7seg_disp_1_f), .a(bcd2_7seg_disp_1_a), .b(bcd2_7seg_disp_1_b),
    .e(bcd2_7seg_disp_1_e), .d(bcd2_7seg_disp_1_d), .c(bcd2_7seg_disp_1_c));  // open: dp
endmodule

module synchronous (
);

  wire and_1_out, and_2_out, and_3_out, and_4_out, and_5_out, and_6_out, and_7_out, bcd2_7seg_disp_1_a,
       bcd2_7seg_disp_1_b, bcd2_7seg_disp_1_c, bcd2_7seg_disp_1_d, bcd2_7seg_disp_1_e, bcd2_7seg_disp_1_f,
       bcd2_7seg_disp_1_g, clock_1_out, d_ff_1_q, d_ff_2_q, d_ff_3_q, d_ff_4_q, not_1_out, not_2_out,
       not_3_out, not_4_out, not_5_out, not_6_out, not_7_out, not_8_out, or_1_out, or_2_out, or_3_out;

  not not_1 (not_1_out, d_ff_4_q);
  not not_2 (not_2_out, d_ff_2_q);
  not not_3 (not_3_out, d_ff_3_q);
  not not_4 (not_4_out, d_ff_4_q);
  not not_5 (not_5_out, d_ff_1_q);
  not not_6 (not_6_out, d_ff_3_q);
  not not_7 (not_7_out, d_ff_4_q);
  not not_8 (not_8_out, d_ff_4_q);
  and and_1 (and_1_out, d_ff_2_q, d_ff_3_q, d_ff_4_q);
  or or_1 (or_1_out, and_1_out, and_2_out);
  and and_2 (and_2_out, d_ff_1_q, not_1_out);
  and and_3 (and_3_out, not_2_out, d_ff_3_q, d_ff_4_q);
  or or_2 (or_2_out, and_3_out, and_4_out, and_5_out);
  and and_4 (and_4_out, d_ff_2_q, not_3_out);
  and and_5 (and_5_out, d_ff_2_q, not_4_out);
  and and_6 (and_6_out, not_5_out, not_6_out, d_ff_4_q);
  or or_3 (or_3_out, and_6_out, and_7_out);
  and and_7 (and_7_out, d_ff_3_q, not_7_out);
  Clock clock_1 (.out(clock_1_out));
  D_Flip_Flop #(.trigger("falling")) d_ff_1 (
    .clk(clock_1_out), .D(or_1_out), .Q(d_ff_1_q));  // open: Qn, preset, en, reset
  D_Flip_Flop #(.trigger("falling")) d_ff_2 (
    .clk(clock_1_out), .D(or_2_out), .Q(d_ff_2_q));  // open: Qn, preset, en, reset
  D_Flip_Flop #(.trigger("falling")) d_ff_3 (
    .clk(clock_1_out), .D(or_3_out), .Q(d_ff_3_q));  // open: Qn, preset, en, reset
  D_Flip_Flop #(.trigger("falling")) d_ff_4 (
    .clk(clock_1_out), .D(not_8_out), .Q(d_ff_4_q));  // open: Qn, preset, en, reset
  bcd2_7seg_disp bcd2_7seg_disp_1 (
    .X3(d_ff_1_q), .X2(d_ff_2_q), .X1(d_ff_3_q), .X0(d_ff_4_q), .a(bcd2_7seg_disp_1_a),
    .b(bcd2_7seg_disp_1_b), .c(bcd2_7seg_disp_1_c), .d(bcd2_7seg_disp_1_d), .e(bcd2_7seg_disp_1_e),
    .f(bcd2_7seg_disp_1_f), .g(bcd2_7seg_disp_1_g));
  _7_Segment_Display u_7_segment_display_1 (
    .g(bcd2_7seg_disp_1_g), .f(bcd2_7seg_disp_1_f), .a(bcd2_7seg_disp_1_a), .b(bcd2_7seg_disp_1_b),
    .e(bcd2_7seg_disp_1_e), .d(bcd2_7seg_disp_1_d), .c(bcd2_7seg_disp_1_c));  // open: dp
endmodule

module random_asynchronous (
);

  wire and_1_out, and_2_out, and_3_out, and_4_out, and_5_out, and_6_out, bcd2_7seg_disp_1_a,
       bcd2_7seg_disp_1_b, bcd2_7seg_disp_1_c, bcd2_7seg_disp_1_d, bcd2_7seg_disp_1_e, bcd2_7seg_disp_1_f,
       bcd2_7seg_disp_1_g, j_k_ff_1_q, j_k_ff_2_q, j_k_ff_3_q, j_k_ff_4_q, not_1_out, not_2_out, not_3_out,
       not_4_out, not_5_out, not_6_out, or_1_out, or_2_out, or_3_out;

  and and_1 (and_1_out, j_k_ff_2_q, j_k_ff_3_q, j_k_ff_4_q);
  not not_1 (not_1_out, j_k_ff_2_q);
  not not_2 (not_2_out, j_k_ff_3_q);
  not not_3 (not_3_out, j_k_ff_4_q);
  not not_4 (not_4_out, j_k_ff_3_q);
  not not_5 (not_5_out, j_k_ff_4_q);
  not not_6 (not_6_out, j_k_ff_4_q);
  or or_1 (or_1_out, and_1_out, j_k_ff_1_q);
  and and_2 (and_2_out, not_1_out, j_k_ff_3_q, j_k_ff_4_q);
  and and_3 (and_3_out, j_k_ff_2_q, not_2_out);
  and and_4 (and_4_out, j_k_ff_2_q, not_3_out);
  and and_5 (and_5_out, not_4_out, j_k_ff_4_q);
  and and_6 (and_6_out, j_k_ff_3_q, not_5_out);
  or or_2 (or_2_out, and_2_out, and_3_out, and_4_out);
  or or_3 (or_3_out, and_5_out, and_6_out);
  J_K_Flip_Flop j_k_ff_1 (.J(or_1_out), .K(or_1_out), .Q(j_k_ff_1_q));  // open: clk, Qn, preset, en, reset
  J_K_Flip_Flop j_k_ff_2 (.J(or_2_out), .K(or_2_out), .Q(j_k_ff_2_q));  // open: clk, Qn, preset, en, reset
  J_K_Flip_Flop j_k_ff_3 (.K(or_3_out), .Q(j_k_ff_3_q));  // open: J, clk, Qn, preset, en, reset
  J_K_Flip_Flop j_k_ff_4 (.J(not_6_out), .K(not_6_out), .Q(j_k_ff_4_q));  // open: clk, Qn, preset, en, reset
  _7_Segment_Display u_7_segment_display_1 (
    .g(bcd2_7seg_disp_1_g), .f(bcd2_7seg_disp_1_f), .a(bcd2_7seg_disp_1_a), .b(bcd2_7seg_disp_1_b),
    .e(bcd2_7seg_disp_1_e), .d(bcd2_7seg_disp_1_d), .c(bcd2_7seg_disp_1_c));  // open: dp
  bcd2_7seg_disp bcd2_7seg_disp_1 (
    .X3(j_k_ff_1_q), .X2(j_k_ff_2_q), .X1(j_k_ff_3_q), .X0(j_k_ff_4_q), .a(bcd2_7seg_disp_1_a),
    .b(bcd2_7seg_disp_1_b), .c(bcd2_7seg_disp_1_c), .d(bcd2_7seg_disp_1_d), .e(bcd2_7seg_disp_1_e),
    .f(bcd2_7seg_disp_1_f), .g(bcd2_7seg_disp_1_g));
endmodule

module synchronous_down (
);

  wire and_1_out, and_2_out, and_3_out, and_4_out, and_5_out, and_6_out, and_7_out, and_8_out,
       bcd2_7seg_disp_1_a, bcd2_7seg_disp_1_b, bcd2_7seg_disp_1_c, bcd2_7seg_disp_1_d, bcd2_7seg_disp_1_e,
       bcd2_7seg_disp_1_f, bcd2_7seg_disp_1_g, clock_1_out, d_ff_1_q, d_ff_2_q, d_ff_3_q, d_ff_4_q,
       not_1_out, not_2_out, not_3_out, not_4_out, not_5_out, not_6_out, not_7_out, not_8_out, not_9_out,
       or_1_out, or_2_out, or_3_out;

  not not_1 (not_1_out, d_ff_1_q);
  not not_2 (not_2_out, d_ff_2_q);
  not not_3 (not_3_out, d_ff_3_q);
  not not_4 (not_4_out, d_ff_4_q);
  not not_5 (not_5_out, d_ff_4_q);
  not not_6 (not_6_out, d_ff_3_q);
  not not_7 (not_7_out, d_ff_4_q);
  not not_8 (not_8_out, d_ff_4_q);
  not not_9 (not_9_out, d_ff_4_q);
  and and_1 (and_1_out, not_1_out, not_2_out, not_3_out, not_4_out);
  and and_2 (and_2_out, d_ff_1_q, d_ff_4_q);
  and and_3 (and_3_out, d_ff_2_q, d_ff_4_q);
  and and_4 (and_4_out, d_ff_2_q, d_ff_3_q);
  and and_5 (and_5_out, d_ff_1_q, not_5_out);
  and and_6 (and_6_out, d_ff_3_q, d_ff_4_q);
  and and_7 (and_7_out, d_ff_2_q, not_6_out, not_7_out);
  and and_8 (and_8_out, d_ff_1_q, not_8_out);
  or or_1 (or_1_out, and_1_out, and_2_out);
  or or_2 (or_2_out, and_3_out, and_4_out, and_5_out);
  or or_3 (or_3_out, and_6_out, and_7_out, and_8_out);
  Clock clock_1 (.out(clock_1_out));
  D_Flip_Flop d_ff_1 (.clk(clock_1_out), .D(or_1_out), .Q(d_ff_1_q));  // open: Qn, preset, en, reset
  D_Flip_Flop d_ff_2 (.clk(clock_1_out), .D(or_2_out), .Q(d_ff_2_q));  // open: Qn, preset, en, reset
  D_Flip_Flop d_ff_3 (.clk(clock_1_out), .D(or_3_out), .Q(d_ff_3_q));  // open: Qn, preset, en, reset
  D_Flip_Flop d_ff_4 (.clk(clock_1_out), .D(not_9_out), .Q(d_ff_4_q));  // open: Qn, preset, en, reset
  _7_Segment_Display u_7_segment_display_1 (
    .g(bcd2_7seg_disp_1_g), .f(bcd2_7seg_disp_1_f), .a(bcd2_7seg_disp_1_a), .b(bcd2_7seg_disp_1_b),
    .e(bcd2_7seg_disp_1_e), .d(bcd2_7seg_disp_1_d), .c(bcd2_7seg_disp_1_c));  // open: dp
  bcd2_7seg_disp bcd2_7seg_disp_1 (
    .X3(d_ff_1_q), .X2(d_ff_2_q), .X1(d_ff_3_q), .X0(d_ff_4_q), .a(bcd2_7seg_disp_1_a),
    .b(bcd2_7seg_disp_1_b), .c(bcd2_7seg_disp_1_c), .d(bcd2_7seg_disp_1_d), .e(bcd2_7seg_disp_1_e),
    .f(bcd2_7seg_disp_1_f), .g(bcd2_7seg_disp_1_g));
endmodule

module random_sequence (
);

  wire and_1_out, and_2_out, and_3_out, and_4_out, bcd2_7seg_disp_1_a, bcd2_7seg_disp_1_b,
       bcd2_7seg_disp_1_c, bcd2_7seg_disp_1_d, bcd2_7seg_disp_1_e, bcd2_7seg_disp_1_f, bcd2_7seg_disp_1_g,
       clock_1_out, d_ff_1_q, d_ff_2_q, d_ff_3_q, d_ff_4_q, not_1_out, not_2_out, not_3_out, not_4_out,
       not_5_out, or_1_out, or_2_out;

  not not_1 (not_1_out, d_ff_2_q);
  not not_2 (not_2_out, d_ff_4_q);
  not not_3 (not_3_out, d_ff_4_q);
  not not_4 (not_4_out, d_ff_2_q);
  not not_5 (not_5_out, d_ff_4_q);
  and and_1 (and_1_out, not_1_out, d_ff_4_q);
  and and_2 (and_2_out, d_ff_2_q, not_2_out);
  and and_3 (and_3_out, d_ff_2_q, not_3_out);
  and and_4 (and_4_out, not_4_out, not_5_out);
  or or_1 (or_1_out, and_1_out, d_ff_3_q, and_2_out);
  or or_2 (or_2_out, and_4_out, d_ff_3_q);
  Clock clock_1 (.out(clock_1_out));
  D_Flip_Flop d_ff_1 (.clk(clock_1_out), .D(d_ff_1_q), .Q(d_ff_1_q));  // open: Qn, preset, en, reset
  D_Flip_Flop d_ff_2 (.clk(clock_1_out), .D(or_1_out), .Q(d_ff_2_q));  // open: Qn, preset, en, reset
  D_Flip_Flop d_ff_3 (.clk(clock_1_out), .D(and_3_out), .Q(d_ff_3_q));  // open: Qn, preset, en, reset
  D_Flip_Flop d_ff_4 (.clk(clock_1_out), .D(or_2_out), .Q(d_ff_4_q));  // open: Qn, preset, en, reset
  bcd2_7seg_disp bcd2_7seg_disp_1 (
    .X3(d_ff_1_q), .X2(d_ff_2_q), .X1(d_ff_3_q), .X0(d_ff_4_q), .a(bcd2_7seg_disp_1_a),
    .b(bcd2_7seg_disp_1_b), .c(bcd2_7seg_disp_1_c), .d(bcd2_7seg_disp_1_d), .e(bcd2_7seg_disp_1_e),
    .f(bcd2_7seg_disp_1_f), .g(bcd2_7seg_disp_1_g));
  _7_Segment_Display u_7_segment_display_1 (
    .g(bcd2_7seg_disp_1_g), .f(bcd2_7seg_disp_1_f), .a(bcd2_7seg_disp_1_a), .b(bcd2_7seg_disp_1_b),
    .e(bcd2_7seg_disp_1_e), .d(bcd2_7seg_disp_1_d), .c(bcd2_7seg_disp_1_c));  // open: dp
  // also tied to GND on the sheet: d_ff_1_q
endmodule

module up_down_synchronous (
);

  wire and_1_out, and_2_out, and_3_out, and_4_out, and_5_out, and_6_out, and_7_out, and_8_out, and_9_out,
       bcd2_7seg_disp_1_a, bcd2_7seg_disp_1_b, bcd2_7seg_disp_1_c, bcd2_7seg_disp_1_d, bcd2_7seg_disp_1_e,
       bcd2_7seg_disp_1_f, bcd2_7seg_disp_1_g, clock_1_out, d_ff_1_q, d_ff_2_q, d_ff_3_q, d_ff_4_q,
       not_1_out, not_2_out, not_3_out, not_4_out, not_5_out, not_6_out, not_7_out, not_8_out, not_9_out,
       not_10_out, not_11_out, not_12_out, not_13_out, not_14_out, not_15_out, or_1_out, or_2_out;

  not not_1 (not_1_out, d_ff_1_q);
  not not_2 (not_2_out, d_ff_2_q);
  not not_3 (not_3_out, d_ff_2_q);
  not not_4 (not_4_out, d_ff_3_q);
  not not_5 (not_5_out, d_ff_4_q);
  not not_6 (not_6_out, d_ff_1_q);
  not not_7 (not_7_out, d_ff_3_q);
  not not_8 (not_8_out, d_ff_1_q);
  not not_9 (not_9_out, d_ff_4_q);
  not not_10 (not_10_out, d_ff_3_q);
  not not_11 (not_11_out, d_ff_4_q);
  not not_12 (not_12_out, d_ff_4_q);
  and and_1 (and_1_out, not_1_out, not_2_out, d_ff_3_q, d_ff_4_q);
  not not_13 (not_13_out, d_ff_1_q);
  and and_2 (and_2_out, not_13_out, d_ff_2_q, not_14_out);
  not not_14 (not_14_out, d_ff_3_q);
  and and_3 (and_3_out, d_ff_2_q, d_ff_3_q, not_15_out);
  not not_15 (not_15_out, d_ff_4_q);
  and and_4 (and_4_out, d_ff_1_q, not_3_out, not_4_out, not_5_out);
  and and_5 (and_5_out, d_ff_1_q, d_ff_2_q, d_ff_4_q);
  and and_6 (and_6_out, not_6_out, not_7_out, d_ff_4_q);
  and and_7 (and_7_out, not_8_out, d_ff_3_q, not_9_out);
  and and_8 (and_8_out, d_ff_1_q, not_10_out, not_11_out);
  and and_9 (and_9_out, d_ff_1_q, d_ff_3_q, d_ff_4_q);
  or or_1 (or_1_out, and_1_out, and_2_out, and_3_out, and_4_out, and_5_out);
  or or_2 (or_2_out, and_6_out, and_7_out, and_8_out, and_9_out);
  Clock clock_1 (.out(clock_1_out));
  D_Flip_Flop d_ff_1 (.clk(clock_1_out), .D(1'b1), .Q(d_ff_1_q));  // open: Qn, preset, en, reset
  D_Flip_Flop d_ff_2 (.clk(clock_1_out), .D(or_1_out), .Q(d_ff_2_q));  // open: Qn, preset, en, reset
  D_Flip_Flop d_ff_3 (.clk(clock_1_out), .D(or_2_out), .Q(d_ff_3_q));  // open: Qn, preset, en, reset
  D_Flip_Flop d_ff_4 (.clk(clock_1_out), .D(not_12_out), .Q(d_ff_4_q));  // open: Qn, preset, en, reset
  _7_Segment_Display u_7_segment_display_1 (
    .g(bcd2_7seg_disp_1_g), .f(bcd2_7seg_disp_1_f), .a(bcd2_7seg_disp_1_a), .b(bcd2_7seg_disp_1_b),
    .e(bcd2_7seg_disp_1_e), .d(bcd2_7seg_disp_1_d), .c(bcd2_7seg_disp_1_c));  // open: dp
  bcd2_7seg_disp bcd2_7seg_disp_1 (
    .X3(d_ff_1_q), .X2(d_ff_2_q), .X1(d_ff_3_q), .X0(d_ff_4_q), .a(bcd2_7seg_disp_1_a),
    .b(bcd2_7seg_disp_1_b), .c(bcd2_7seg_disp_1_c), .d(bcd2_7seg_disp_1_d), .e(bcd2_7seg_disp_1_e),
    .f(bcd2_7seg_disp_1_f), .g(bcd2_7seg_disp_1_g));
endmodule

module random_synchronous_2 (
);

  wire and_1_out, and_2_out, and_3_out, and_4_out, bcd2_7seg_disp_1_a, bcd2_7seg_disp_1_b,
       bcd2_7seg_disp_1_c, bcd2_7seg_disp_1_d, bcd2_7seg_disp_1_e, bcd2_7seg_disp_1_f, bcd2_7seg_disp_1_g,
       clock_1_out, d_ff_1_q, d_ff_2_q, d_ff_3_q, d_ff_4_q, not_1_out, not_2_out, not_3_out, not_4_out,
       not_5_out, not_6_out, not_7_out, or_1_out, or_2_out, or_3_out;

  not not_1 (not_1_out, d_ff_3_q);
  not not_2 (not_2_out, d_ff_3_q);
  not not_3 (not_3_out, d_ff_4_q);
  not not_4 (not_4_out, d_ff_2_q);
  not not_5 (not_5_out, d_ff_4_q);
  not not_6 (not_6_out, d_ff_3_q);
  not not_7 (not_7_out, d_ff_4_q);
  or or_1 (or_1_out, not_1_out, d_ff_4_q);
  and and_1 (and_1_out, not_2_out, d_ff_4_q);
  or or_2 (or_2_out, and_1_out, and_2_out);
  and and_2 (and_2_out, d_ff_3_q, not_3_out);
  and and_3 (and_3_out, not_4_out, not_5_out);
  or or_3 (or_3_out, and_3_out, and_4_out);
  and and_4 (and_4_out, not_6_out, not_7_out);
  Clock clock_1 (.out(clock_1_out));
  D_Flip_Flop d_ff_1 (.clk(clock_1_out), .D(d_ff_1_q), .Q(d_ff_1_q));  // open: Qn, preset, en, reset
  D_Flip_Flop d_ff_2 (.clk(clock_1_out), .D(or_1_out), .Q(d_ff_2_q));  // open: Qn, preset, en, reset
  D_Flip_Flop d_ff_3 (.clk(clock_1_out), .D(or_2_out), .Q(d_ff_3_q));  // open: Qn, preset, en, reset
  D_Flip_Flop d_ff_4 (.clk(clock_1_out), .D(or_3_out), .Q(d_ff_4_q));  // open: Qn, preset, en, reset
  _7_Segment_Display u_7_segment_display_1 (
    .g(bcd2_7seg_disp_1_g), .f(bcd2_7seg_disp_1_f), .a(bcd2_7seg_disp_1_a), .b(bcd2_7seg_disp_1_b),
    .e(bcd2_7seg_disp_1_e), .d(bcd2_7seg_disp_1_d), .c(bcd2_7seg_disp_1_c));  // open: dp
  bcd2_7seg_disp bcd2_7seg_disp_1 (
    .X3(d_ff_1_q), .X2(d_ff_2_q), .X1(d_ff_3_q), .X0(d_ff_4_q), .a(bcd2_7seg_disp_1_a),
    .b(bcd2_7seg_disp_1_b), .c(bcd2_7seg_disp_1_c), .d(bcd2_7seg_disp_1_d), .e(bcd2_7seg_disp_1_e),
    .f(bcd2_7seg_disp_1_f), .g(bcd2_7seg_disp_1_g));
  // also tied to GND on the sheet: d_ff_1_q
endmodule

module mod_6_asynchronous (
  input  in_1
);

  wire and_1_out, bcd2_7seg_disp_1_a, bcd2_7seg_disp_1_b, bcd2_7seg_disp_1_c, bcd2_7seg_disp_1_d,
       bcd2_7seg_disp_1_e, bcd2_7seg_disp_1_f, bcd2_7seg_disp_1_g, clock_1_out, j_k_ff_1_q, j_k_ff_2_q,
       j_k_ff_3_q;

  Clock clock_1 (.out(clock_1_out));
  J_K_Flip_Flop #(.trigger("falling")) j_k_ff_1 (
    .J(1'b1), .clk(clock_1_out), .K(1'b1), .Q(j_k_ff_1_q), .reset(and_1_out));  // open: Qn, preset, en
  J_K_Flip_Flop #(.trigger("falling")) j_k_ff_2 (
    .J(1'b1), .clk(j_k_ff_1_q), .K(1'b1), .Q(j_k_ff_2_q), .reset(and_1_out));  // open: Qn, preset, en
  J_K_Flip_Flop #(.trigger("falling")) j_k_ff_3 (
    .J(1'b1), .clk(j_k_ff_2_q), .K(1'b1), .Q(j_k_ff_3_q), .reset(and_1_out));  // open: Qn, preset, en
  and and_1 (and_1_out, j_k_ff_2_q, j_k_ff_3_q);
  bcd2_7seg_disp bcd2_7seg_disp_1 (
    .X3(in_1), .X2(j_k_ff_3_q), .X1(j_k_ff_2_q), .X0(j_k_ff_1_q), .a(bcd2_7seg_disp_1_a),
    .b(bcd2_7seg_disp_1_b), .c(bcd2_7seg_disp_1_c), .d(bcd2_7seg_disp_1_d), .e(bcd2_7seg_disp_1_e),
    .f(bcd2_7seg_disp_1_f), .g(bcd2_7seg_disp_1_g));
  _7_Segment_Display u_7_segment_display_1 (
    .g(bcd2_7seg_disp_1_g), .f(bcd2_7seg_disp_1_f), .a(bcd2_7seg_disp_1_a), .b(bcd2_7seg_disp_1_b),
    .e(bcd2_7seg_disp_1_e), .d(bcd2_7seg_disp_1_d), .c(bcd2_7seg_disp_1_c));  // open: dp
endmodule

module modulo_8 (
);

  wire and_1_out, and_2_out, and_3_out, and_4_out, and_5_out, and_6_out, and_7_out, bcd2_7seg_disp_1_a,
       bcd2_7seg_disp_1_b, bcd2_7seg_disp_1_c, bcd2_7seg_disp_1_d, bcd2_7seg_disp_1_e, bcd2_7seg_disp_1_f,
       bcd2_7seg_disp_1_g, clock_1_out, d_ff_1_q, d_ff_2_q, d_ff_3_q, d_ff_4_q, not_1_out, not_2_out,
       not_3_out, not_4_out, not_5_out, not_6_out, not_7_out, or_1_out, or_2_out;

  not not_1 (not_1_out, d_ff_2_q);
  not not_2 (not_2_out, d_ff_3_q);
  not not_3 (not_3_out, d_ff_4_q);
  not not_4 (not_4_out, d_ff_3_q);
  not not_5 (not_5_out, d_ff_4_q);
  not not_6 (not_6_out, d_ff_1_q);
  not not_7 (not_7_out, d_ff_4_q);
  and and_1 (and_1_out, d_ff_2_q, d_ff_3_q, d_ff_4_q);
  and and_2 (and_2_out, not_1_out, d_ff_3_q, d_ff_4_q);
  and and_3 (and_3_out, d_ff_2_q, not_2_out);
  and and_4 (and_4_out, d_ff_2_q, not_3_out);
  and and_5 (and_5_out, not_4_out, d_ff_4_q);
  and and_6 (and_6_out, d_ff_3_q, not_5_out);
  and and_7 (and_7_out, not_6_out, not_7_out);
  or or_1 (or_1_out, and_2_out, and_3_out, and_4_out);
  or or_2 (or_2_out, and_5_out, and_6_out);
  Clock clock_1 (.out(clock_1_out));
  D_Flip_Flop d_ff_1 (.clk(clock_1_out), .D(and_1_out), .Q(d_ff_1_q));  // open: Qn, preset, en, reset
  D_Flip_Flop d_ff_2 (.clk(clock_1_out), .D(or_1_out), .Q(d_ff_2_q));  // open: Qn, preset, en, reset
  D_Flip_Flop d_ff_3 (.clk(clock_1_out), .D(or_2_out), .Q(d_ff_3_q));  // open: Qn, preset, en, reset
  D_Flip_Flop d_ff_4 (.clk(clock_1_out), .D(and_7_out), .Q(d_ff_4_q));  // open: Qn, preset, en, reset
  _7_Segment_Display u_7_segment_display_1 (
    .g(bcd2_7seg_disp_1_g), .f(bcd2_7seg_disp_1_f), .a(bcd2_7seg_disp_1_a), .b(bcd2_7seg_disp_1_b),
    .e(bcd2_7seg_disp_1_e), .d(bcd2_7seg_disp_1_d), .c(bcd2_7seg_disp_1_c));  // open: dp
  bcd2_7seg_disp bcd2_7seg_disp_1 (
    .X3(d_ff_1_q), .X2(d_ff_2_q), .X1(d_ff_3_q), .X0(d_ff_4_q), .a(bcd2_7seg_disp_1_a),
    .b(bcd2_7seg_disp_1_b), .c(bcd2_7seg_disp_1_c), .d(bcd2_7seg_disp_1_d), .e(bcd2_7seg_disp_1_e),
    .f(bcd2_7seg_disp_1_f), .g(bcd2_7seg_disp_1_g));
endmodule

module modulo_8_ripple_counter (
  input  in_1,
  input  in_2
);

  wire bcd2_7seg_disp_1_a, bcd2_7seg_disp_1_b, bcd2_7seg_disp_1_c, bcd2_7seg_disp_1_d, bcd2_7seg_disp_1_e,
       bcd2_7seg_disp_1_f, bcd2_7seg_disp_1_g, clock_1_out, j_k_ff_1_q, j_k_ff_2_q, j_k_ff_3_q, xor_1_out,
       xor_2_out;

  Clock clock_1 (.out(clock_1_out));
  J_K_Flip_Flop #(.trigger("falling")) j_k_ff_1 (
    .J(1'b1), .clk(clock_1_out), .K(1'b1), .Q(j_k_ff_1_q));  // open: Qn, preset, en, reset
  xor xor_1 (xor_1_out, j_k_ff_1_q, 1'b1);
  J_K_Flip_Flop #(.trigger("falling")) j_k_ff_2 (
    .J(1'b1), .clk(xor_1_out), .K(1'b1), .Q(j_k_ff_2_q));  // open: Qn, preset, en, reset
  xor xor_2 (xor_2_out, j_k_ff_2_q, 1'b1);
  J_K_Flip_Flop #(.trigger("falling")) j_k_ff_3 (
    .J(1'b1), .clk(xor_2_out), .K(1'b1), .Q(j_k_ff_3_q));  // open: Qn, preset, en, reset
  bcd2_7seg_disp bcd2_7seg_disp_1 (
    .X3(in_1), .X2(j_k_ff_3_q), .X1(j_k_ff_2_q), .X0(j_k_ff_1_q), .a(bcd2_7seg_disp_1_a),
    .b(bcd2_7seg_disp_1_b), .c(bcd2_7seg_disp_1_c), .d(bcd2_7seg_disp_1_d), .e(bcd2_7seg_disp_1_e),
    .f(bcd2_7seg_disp_1_f), .g(bcd2_7seg_disp_1_g));
  _7_Segment_Display u_7_segment_display_1 (
    .g(bcd2_7seg_disp_1_g), .f(bcd2_7seg_disp_1_f), .a(bcd2_7seg_disp_1_a), .b(bcd2_7seg_disp_1_b),
    .e(bcd2_7seg_disp_1_e), .d(bcd2_7seg_disp_1_d), .c(bcd2_7seg_disp_1_c));  // open: dp
endmodule

module modulo_5_asynch_DFF (
  input  in_1
);

  wire and_1_out, and_2_out, and_3_out, and_4_out, bcd2_7seg_disp_1_a, bcd2_7seg_disp_1_b,
       bcd2_7seg_disp_1_c, bcd2_7seg_disp_1_d, bcd2_7seg_disp_1_e, bcd2_7seg_disp_1_f, bcd2_7seg_disp_1_g,
       clock_1_out, d_ff_1_q, d_ff_2_q, d_ff_3_q, not_1_out, not_2_out, not_3_out, not_4_out, or_1_out;

  and and_1 (and_1_out, d_ff_2_q, d_ff_1_q);
  not not_1 (not_1_out, d_ff_2_q);
  not not_2 (not_2_out, d_ff_1_q);
  not not_3 (not_3_out, d_ff_3_q);
  not not_4 (not_4_out, d_ff_1_q);
  Clock clock_1 (.out(clock_1_out));
  and and_2 (and_2_out, not_1_out, d_ff_1_q);
  and and_3 (and_3_out, d_ff_2_q, not_2_out);
  and and_4 (and_4_out, not_3_out, not_4_out);
  D_Flip_Flop #(.trigger("falling")) d_ff_1 (
    .clk(clock_1_out), .D(and_4_out), .Q(d_ff_1_q));  // open: Qn, preset, en, reset
  or or_1 (or_1_out, and_2_out, and_3_out);
  D_Flip_Flop #(.trigger("falling")) d_ff_2 (
    .clk(d_ff_1_q), .D(or_1_out), .Q(d_ff_2_q));  // open: Qn, preset, en, reset
  D_Flip_Flop #(.trigger("falling")) d_ff_3 (
    .clk(d_ff_2_q), .D(and_1_out), .Q(d_ff_3_q));  // open: Qn, preset, en, reset
  _7_Segment_Display u_7_segment_display_1 (
    .g(bcd2_7seg_disp_1_g), .f(bcd2_7seg_disp_1_f), .a(bcd2_7seg_disp_1_a), .b(bcd2_7seg_disp_1_b),
    .e(bcd2_7seg_disp_1_e), .d(bcd2_7seg_disp_1_d), .c(bcd2_7seg_disp_1_c));  // open: dp
  bcd2_7seg_disp bcd2_7seg_disp_1 (
    .X3(in_1), .X2(and_1_out), .X1(or_1_out), .X0(and_4_out), .a(bcd2_7seg_disp_1_a), .b(bcd2_7seg_disp_1_b),
    .c(bcd2_7seg_disp_1_c), .d(bcd2_7seg_disp_1_d), .e(bcd2_7seg_disp_1_e), .f(bcd2_7seg_disp_1_f),
    .g(bcd2_7seg_disp_1_g));
endmodule

module mod_11_async_DFF (
);

  wire and_1_out, and_2_out, and_3_out, and_4_out, and_5_out, and_6_out, bcd2_7seg_disp_1_a,
       bcd2_7seg_disp_1_b, bcd2_7seg_disp_1_c, bcd2_7seg_disp_1_d, bcd2_7seg_disp_1_e, bcd2_7seg_disp_1_f,
       bcd2_7seg_disp_1_g, clock_1_out, d_ff_1_q, d_ff_2_q, d_ff_3_q, d_ff_4_q, not_1_out, not_2_out,
       not_3_out, not_4_out, not_5_out, not_6_out, or_1_out, or_2_out, or_3_out;

  and and_1 (and_1_out, d_ff_2_q, d_ff_3_q, d_ff_4_q);
  not not_1 (not_1_out, d_ff_2_q);
  not not_2 (not_2_out, d_ff_3_q);
  not not_3 (not_3_out, d_ff_4_q);
  not not_4 (not_4_out, d_ff_3_q);
  not not_5 (not_5_out, d_ff_4_q);
  not not_6 (not_6_out, d_ff_4_q);
  or or_1 (or_1_out, and_1_out, d_ff_1_q);
  and and_2 (and_2_out, not_1_out, d_ff_3_q, d_ff_4_q);
  and and_3 (and_3_out, d_ff_2_q, not_2_out);
  and and_4 (and_4_out, d_ff_2_q, not_3_out);
  and and_5 (and_5_out, not_4_out, d_ff_4_q);
  and and_6 (and_6_out, d_ff_3_q, not_5_out);
  or or_2 (or_2_out, and_2_out, and_3_out, and_4_out);
  or or_3 (or_3_out, and_5_out, and_6_out);
  Clock clock_1 (.out(clock_1_out));
  D_Flip_Flop #(.trigger("falling")) d_ff_1 (
    .clk(d_ff_2_q), .D(or_1_out), .Q(d_ff_1_q));  // open: Qn, preset, en, reset
  D_Flip_Flop #(.trigger("falling")) d_ff_2 (
    .clk(d_ff_3_q), .D(or_2_out), .Q(d_ff_2_q));  // open: Qn, preset, en, reset
  D_Flip_Flop #(.trigger("falling")) d_ff_3 (
    .clk(d_ff_4_q), .D(or_3_out), .Q(d_ff_3_q));  // open: Qn, preset, en, reset
  D_Flip_Flop #(.trigger("falling")) d_ff_4 (
    .clk(clock_1_out), .D(not_6_out), .Q(d_ff_4_q));  // open: Qn, preset, en, reset
  bcd2_7seg_disp bcd2_7seg_disp_1 (
    .X3(d_ff_1_q), .X2(d_ff_2_q), .X1(d_ff_3_q), .X0(d_ff_4_q), .a(bcd2_7seg_disp_1_a),
    .b(bcd2_7seg_disp_1_b), .c(bcd2_7seg_disp_1_c), .d(bcd2_7seg_disp_1_d), .e(bcd2_7seg_disp_1_e),
    .f(bcd2_7seg_disp_1_f), .g(bcd2_7seg_disp_1_g));
  _7_Segment_Display u_7_segment_display_1 (
    .g(bcd2_7seg_disp_1_g), .f(bcd2_7seg_disp_1_f), .a(bcd2_7seg_disp_1_a), .b(bcd2_7seg_disp_1_b),
    .e(bcd2_7seg_disp_1_e), .d(bcd2_7seg_disp_1_d), .c(bcd2_7seg_disp_1_c));  // open: dp
endmodule

module number_of_1_s (
  input  clock,
  output c,
  output b,
  output a
);

  J_K_Flip_Flop #(.trigger("falling")) j_k_ff_1 (
    .J(1'b1), .clk(clock), .K(1'b1), .Q(c));  // open: Qn, preset, en, reset
  J_K_Flip_Flop #(.trigger("falling")) j_k_ff_2 (.J(1'b1), .clk(c), .K(1'b1), .Q(b));  // open: Qn, preset, en, reset
  J_K_Flip_Flop #(.trigger("falling")) j_k_ff_3 (.J(1'b1), .clk(b), .K(1'b1), .Q(a));  // open: Qn, preset, en, reset
endmodule

module number_of_1_ss (
  input  in_1,
  input  in_2
);

  wire and_1_out, and_2_out, and_3_out, and_4_out, and_5_out, and_6_out, and_7_out, bcd2_7seg_disp_1_a,
       bcd2_7seg_disp_1_b, bcd2_7seg_disp_1_c, bcd2_7seg_disp_1_d, bcd2_7seg_disp_1_e, bcd2_7seg_disp_1_f,
       bcd2_7seg_disp_1_g, clock_1_out, not_1_out, not_2_out, not_3_out, not_4_out, not_5_out, not_6_out,
       number_of_1_s_1_a, number_of_1_s_1_b, number_of_1_s_1_c, or_1_out, or_2_out;

  number_of_1_s number_of_1_s_1 (
    .clock(clock_1_out), .c(number_of_1_s_1_c), .b(number_of_1_s_1_b), .a(number_of_1_s_1_a));
  Clock clock_1 (.out(clock_1_out));
  not not_1 (not_1_out, number_of_1_s_1_a);
  not not_2 (not_2_out, number_of_1_s_1_b);
  not not_3 (not_3_out, number_of_1_s_1_a);
  not not_4 (not_4_out, number_of_1_s_1_c);
  not not_5 (not_5_out, number_of_1_s_1_b);
  not not_6 (not_6_out, number_of_1_s_1_c);
  and and_1 (and_1_out, number_of_1_s_1_b, number_of_1_s_1_c);
  and and_2 (and_2_out, number_of_1_s_1_a, number_of_1_s_1_c);
  or or_1 (or_1_out, and_1_out, and_2_out, and_3_out);
  and and_3 (and_3_out, number_of_1_s_1_a, number_of_1_s_1_b);
  and and_4 (and_4_out, not_1_out, not_2_out, number_of_1_s_1_c);
  and and_5 (and_5_out, not_3_out, number_of_1_s_1_b, not_4_out);
  and and_6 (and_6_out, number_of_1_s_1_a, not_5_out, not_6_out);
  and and_7 (and_7_out, number_of_1_s_1_a, number_of_1_s_1_b, number_of_1_s_1_c);
  or or_2 (or_2_out, and_4_out, and_5_out, and_6_out, and_7_out);
  bcd2_7seg_disp bcd2_7seg_disp_1 (
    .X3(in_2), .X2(in_1), .X1(or_1_out), .X0(or_2_out), .a(bcd2_7seg_disp_1_a), .b(bcd2_7seg_disp_1_b),
    .c(bcd2_7seg_disp_1_c), .d(bcd2_7seg_disp_1_d), .e(bcd2_7seg_disp_1_e), .f(bcd2_7seg_disp_1_f),
    .g(bcd2_7seg_disp_1_g));
  _7_Segment_Display u_7_segment_display_1 (
    .g(bcd2_7seg_disp_1_g), .f(bcd2_7seg_disp_1_f), .a(bcd2_7seg_disp_1_a), .b(bcd2_7seg_disp_1_b),
    .e(bcd2_7seg_disp_1_e), .d(bcd2_7seg_disp_1_d), .c(bcd2_7seg_disp_1_c));  // open: dp
endmodule

module grey_code_counter (
  input  in_1
);

  wire and_1_out, and_2_out, and_3_out, and_4_out, and_5_out, and_6_out, bcd2_7seg_disp_1_a,
       bcd2_7seg_disp_1_b, bcd2_7seg_disp_1_c, bcd2_7seg_disp_1_d, bcd2_7seg_disp_1_e, bcd2_7seg_disp_1_f,
       bcd2_7seg_disp_1_g, clock_1_out, d_ff_1_q, d_ff_2_q, d_ff_3_q, not_1_out, not_2_out, not_3_out,
       not_4_out, not_5_out, or_1_out, or_2_out, or_3_out;

  not not_1 (not_1_out, d_ff_3_q);
  not not_2 (not_2_out, d_ff_1_q);
  not not_3 (not_3_out, d_ff_3_q);
  not not_4 (not_4_out, d_ff_1_q);
  not not_5 (not_5_out, d_ff_2_q);
  and and_1 (and_1_out, d_ff_2_q, not_1_out);
  and and_2 (and_2_out, d_ff_1_q, d_ff_3_q);
  and and_3 (and_3_out, not_2_out, d_ff_3_q);
  and and_4 (and_4_out, d_ff_2_q, not_3_out);
  and and_5 (and_5_out, not_4_out, not_5_out);
  and and_6 (and_6_out, d_ff_1_q, d_ff_2_q);
  or or_1 (or_1_out, and_1_out, and_2_out);
  or or_2 (or_2_out, and_3_out, and_4_out);
  or or_3 (or_3_out, and_5_out, and_6_out);
  Clock clock_1 (.out(clock_1_out));
  D_Flip_Flop d_ff_1 (.clk(clock_1_out), .D(or_1_out), .Q(d_ff_1_q));  // open: Qn, preset, en, reset
  D_Flip_Flop d_ff_2 (.clk(clock_1_out), .D(or_2_out), .Q(d_ff_2_q));  // open: Qn, preset, en, reset
  D_Flip_Flop d_ff_3 (.clk(clock_1_out), .D(or_3_out), .Q(d_ff_3_q));  // open: Qn, preset, en, reset
  _7_Segment_Display u_7_segment_display_1 (
    .g(bcd2_7seg_disp_1_g), .f(bcd2_7seg_disp_1_f), .a(bcd2_7seg_disp_1_a), .b(bcd2_7seg_disp_1_b),
    .e(bcd2_7seg_disp_1_e), .d(bcd2_7seg_disp_1_d), .c(bcd2_7seg_disp_1_c));  // open: dp
  bcd2_7seg_disp bcd2_7seg_disp_1 (
    .X3(in_1), .X2(d_ff_1_q), .X1(d_ff_2_q), .X0(d_ff_3_q), .a(bcd2_7seg_disp_1_a), .b(bcd2_7seg_disp_1_b),
    .c(bcd2_7seg_disp_1_c), .d(bcd2_7seg_disp_1_d), .e(bcd2_7seg_disp_1_e), .f(bcd2_7seg_disp_1_f),
    .g(bcd2_7seg_disp_1_g));
endmodule

module prime_counter (
  input  in_1
);

  wire and_1_out, and_2_out, and_3_out, and_4_out, bcd2_7seg_disp_1_a, bcd2_7seg_disp_1_b,
       bcd2_7seg_disp_1_c, bcd2_7seg_disp_1_d, bcd2_7seg_disp_1_e, bcd2_7seg_disp_1_f, bcd2_7seg_disp_1_g,
       clock_1_out, d_ff_1_q, d_ff_2_q, d_ff_3_q, not_1_out, not_2_out, not_3_out, not_4_out, not_5_out,
       or_1_out, or_2_out, or_3_out;

  not not_1 (not_1_out, d_ff_1_q);
  not not_2 (not_2_out, d_ff_2_q);
  not not_3 (not_3_out, d_ff_3_q);
  not not_4 (not_4_out, d_ff_1_q);
  not not_5 (not_5_out, d_ff_2_q);
  and and_1 (and_1_out, not_1_out, d_ff_3_q);
  or or_1 (or_1_out, and_1_out, and_2_out);
  and and_2 (and_2_out, d_ff_1_q, not_2_out);
  or or_2 (or_2_out, not_3_out, d_ff_1_q);
  and and_3 (and_3_out, not_4_out, d_ff_2_q);
  or or_3 (or_3_out, and_3_out, and_4_out);
  and and_4 (and_4_out, d_ff_1_q, not_5_out);
  Clock clock_1 (.out(clock_1_out));
  D_Flip_Flop d_ff_1 (.clk(clock_1_out), .D(or_1_out), .Q(d_ff_1_q));  // open: Qn, preset, en, reset
  D_Flip_Flop d_ff_2 (.clk(clock_1_out), .D(or_2_out), .Q(d_ff_2_q));  // open: Qn, preset, en, reset
  D_Flip_Flop d_ff_3 (.clk(clock_1_out), .D(or_3_out), .Q(d_ff_3_q));  // open: Qn, preset, en, reset
  _7_Segment_Display u_7_segment_display_1 (
    .g(bcd2_7seg_disp_1_g), .f(bcd2_7seg_disp_1_f), .a(bcd2_7seg_disp_1_a), .b(bcd2_7seg_disp_1_b),
    .e(bcd2_7seg_disp_1_e), .d(bcd2_7seg_disp_1_d), .c(bcd2_7seg_disp_1_c));  // open: dp
  bcd2_7seg_disp bcd2_7seg_disp_1 (
    .X3(in_1), .X2(d_ff_1_q), .X1(d_ff_2_q), .X0(d_ff_3_q), .a(bcd2_7seg_disp_1_a), .b(bcd2_7seg_disp_1_b),
    .c(bcd2_7seg_disp_1_c), .d(bcd2_7seg_disp_1_d), .e(bcd2_7seg_disp_1_e), .f(bcd2_7seg_disp_1_f),
    .g(bcd2_7seg_disp_1_g));
endmodule

module _2_in_1 (
  input  in_1
);

  wire and_1_out, and_2_out, and_3_out, and_4_out, and_5_out, and_6_out, and_7_out, and_8_out, and_9_out,
       and_10_out, and_11_out, bcd2_7seg_disp_1_a, bcd2_7seg_disp_1_b, bcd2_7seg_disp_1_c,
       bcd2_7seg_disp_1_d, bcd2_7seg_disp_1_e, bcd2_7seg_disp_1_f, bcd2_7seg_disp_1_g, clock_1_out, d_ff_1_q,
       d_ff_2_q, d_ff_3_q, not_1_out, not_2_out, not_3_out, not_4_out, not_5_out, not_6_out, not_7_out,
       not_8_out, not_9_out, not_10_out, not_11_out, not_12_out, not_13_out, not_14_out, not_15_out,
       or_1_out, or_2_out, or_3_out;

  not not_1 (not_1_out, 1'b1);
  not not_2 (not_2_out, d_ff_1_q);
  not not_3 (not_3_out, 1'b1);
  not not_4 (not_4_out, d_ff_2_q);
  not not_5 (not_5_out, 1'b1);
  not not_6 (not_6_out, d_ff_3_q);
  not not_7 (not_7_out, d_ff_3_q);
  not not_8 (not_8_out, 1'b1);
  and and_1 (and_1_out, not_8_out, not_9_out, d_ff_3_q);
  not not_9 (not_9_out, d_ff_2_q);
  and and_2 (and_2_out, d_ff_2_q, not_10_out);
  not not_10 (not_10_out, d_ff_3_q);
  and and_3 (and_3_out, 1'b1, not_11_out, d_ff_3_q);
  not not_11 (not_11_out, d_ff_1_q);
  not not_12 (not_12_out, 1'b1);
  and and_4 (and_4_out, not_12_out, not_13_out);
  not not_13 (not_13_out, d_ff_3_q);
  not not_14 (not_14_out, d_ff_1_q);
  and and_5 (and_5_out, 1'b1, not_14_out, not_15_out);
  not not_15 (not_15_out, d_ff_2_q);
  and and_6 (and_6_out, 1'b1, d_ff_1_q, d_ff_2_q);
  and and_7 (and_7_out, not_1_out, not_2_out, d_ff_2_q, d_ff_3_q);
  and and_8 (and_8_out, not_3_out, d_ff_1_q, not_4_out);
  and and_9 (and_9_out, not_5_out, d_ff_1_q, not_6_out);
  and and_10 (and_10_out, 1'b1, d_ff_2_q, not_7_out);
  and and_11 (and_11_out, 1'b1, d_ff_1_q, d_ff_3_q);
  or or_1 (or_1_out, and_1_out, and_2_out, and_3_out);
  or or_2 (or_2_out, and_4_out, and_5_out, and_6_out);
  or or_3 (or_3_out, and_7_out, and_8_out, and_9_out, and_10_out, and_11_out);
  Clock clock_1 (.out(clock_1_out));
  D_Flip_Flop d_ff_1 (.clk(clock_1_out), .D(or_3_out), .Q(d_ff_1_q));  // open: Qn, preset, en, reset
  D_Flip_Flop d_ff_2 (.clk(clock_1_out), .D(or_1_out), .Q(d_ff_2_q));  // open: Qn, preset, en, reset
  D_Flip_Flop d_ff_3 (.clk(clock_1_out), .D(or_2_out), .Q(d_ff_3_q));  // open: Qn, preset, en, reset
  bcd2_7seg_disp bcd2_7seg_disp_1 (
    .X3(in_1), .X2(d_ff_1_q), .X1(d_ff_2_q), .X0(d_ff_3_q), .a(bcd2_7seg_disp_1_a), .b(bcd2_7seg_disp_1_b),
    .c(bcd2_7seg_disp_1_c), .d(bcd2_7seg_disp_1_d), .e(bcd2_7seg_disp_1_e), .f(bcd2_7seg_disp_1_f),
    .g(bcd2_7seg_disp_1_g));
  _7_Segment_Display u_7_segment_display_1 (
    .g(bcd2_7seg_disp_1_g), .f(bcd2_7seg_disp_1_f), .a(bcd2_7seg_disp_1_a), .b(bcd2_7seg_disp_1_b),
    .e(bcd2_7seg_disp_1_e), .d(bcd2_7seg_disp_1_d), .c(bcd2_7seg_disp_1_c));  // open: dp
endmodule
