// Logisim project MOD 9 COUNTER.circ as structural Verilog: 1 circuit, main circuit main
module main (
);

  wire clock_1_out, d_ff_1_q, d_ff_2_q, d_ff_4_q, not_1_out, not_2_out, not_3_out;

  not not_1 (not_1_out, d_ff_2_q);
  not not_2 (not_2_out, d_ff_4_q);
  not not_3 (not_3_out, d_ff_1_q);
  // AND_Gate and_1 has open pins: in0=d_ff_1_q, in1=not_1_out, in2=not_2_out, out=open
  Clock clock_1 (.out(clock_1_out));
  D_Flip_Flop d_ff_1 (.clk(clock_1_out), .D(not_3_out), .Q(d_ff_1_q));  // open: Qn, preset, en, reset
  D_Flip_Flop d_ff_2 (.clk(clock_1_out), .Q(d_ff_2_q));  // open: D, Qn, preset, en, reset
  D_Flip_Flop d_ff_3 (.clk(clock_1_out));  // open: D, Q, Qn, preset, en, reset
  D_Flip_Flop d_ff_4 (.clk(clock_1_out), .Q(d_ff_4_q));  // open: D, Qn, preset, en, reset
endmodule
