// Logisim project bcd2_7seg_ diSP.circ as structural Verilog
module BCD2_7SEG (
  output a,
  output b,
  output c,
  output d,
  output e,
  output f,
  output g
);

  wire and_1_out, and_2_out, and_3_out, and_4_out, and_5_out, and_6_out, and_7_out, and_8_out, and_9_out,
       and_10_out, and_11_out, and_12_out, and_13_out, and_14_out, and_15_out, and_16_out, and_17_out,
       and_18_out, and_19_out, and_20_out, and_21_out, and_22_out, and_23_out, and_24_out, and_25_out,
       and_26_out, and_27_out, and_28_out, and_29_out, and_30_out, and_31_out, and_32_out, and_33_out,
       and_34_out, and_35_out, clock_1_out, j_k_ff_1_q, j_k_ff_1_qn, j_k_ff_2_q, j_k_ff_2_qn, j_k_ff_3_q,
       j_k_ff_3_qn, j_k_ff_4_qn, not_1_out, not_2_out, not_3_out, not_4_out, not_5_out, not_6_out, not_7_out,
       not_8_out, not_9_out, not_10_out, not_11_out, not_12_out, not_13_out, not_14_out, not_15_out,
       not_16_out, not_17_out, not_18_out, not_19_out, not_20_out, not_21_out, not_22_out, not_23_out,
       not_24_out, not_25_out, not_26_out, not_27_out, not_28_out, not_29_out, not_30_out, not_31_out,
       not_32_out, not_33_out, not_34_out, not_35_out, not_36_out, not_37_out, not_38_out, not_39_out,
       not_40_out, not_41_out, not_42_out, not_43_out;

  Clock clock_1 (.out(clock_1_out));
  J_K_Flip_Flop j_k_ff_1 (
    .J(1'b1), .clk(clock_1_out), .K(1'b1), .Q(j_k_ff_1_q), .Qn(j_k_ff_1_qn));  // open: preset, en, reset
  J_K_Flip_Flop j_k_ff_2 (
    .J(1'b1), .clk(j_k_ff_1_q), .K(1'b1), .Q(j_k_ff_2_q), .Qn(j_k_ff_2_qn));  // open: preset, en, reset
  J_K_Flip_Flop j_k_ff_3 (
    .J(1'b1), .clk(j_k_ff_2_q), .K(1'b1), .Q(j_k_ff_3_q), .Qn(j_k_ff_3_qn));  // open: preset, en, reset
  J_K_Flip_Flop j_k_ff_4 (.J(1'b1), .clk(j_k_ff_3_q), .K(1'b1), .Qn(j_k_ff_4_qn));  // open: Q, preset, en, reset
  not not_1 (not_1_out, j_k_ff_3_qn);
  not not_2 (not_2_out, j_k_ff_1_qn);
  not not_3 (not_3_out, j_k_ff_4_qn);
  not not_4 (not_4_out, j_k_ff_4_qn);
  not not_5 (not_5_out, j_k_ff_3_qn);
  not not_6 (not_6_out, j_k_ff_2_qn);
  not not_7 (not_7_out, j_k_ff_1_qn);
  not not_8 (not_8_out, j_k_ff_4_qn);
  not not_9 (not_9_out, j_k_ff_3_qn);
  not not_10 (not_10_out, j_k_ff_4_qn);
  not not_11 (not_11_out, j_k_ff_2_qn);
  not not_12 (not_12_out, j_k_ff_1_qn);
  not not_13 (not_13_out, j_k_ff_3_qn);
  not not_14 (not_14_out, j_k_ff_1_qn);
  not not_15 (not_15_out, j_k_ff_4_qn);
  not not_16 (not_16_out, j_k_ff_2_qn);
  not not_17 (not_17_out, j_k_ff_4_qn);
  not not_18 (not_18_out, j_k_ff_2_qn);
  not not_19 (not_19_out, j_k_ff_4_qn);
  not not_20 (not_20_out, j_k_ff_2_qn);
  not not_21 (not_21_out, j_k_ff_4_qn);
  not not_22 (not_22_out, j_k_ff_3_qn);
  not not_23 (not_23_out, j_k_ff_4_qn);
  not not_24 (not_24_out, j_k_ff_3_qn);
  not not_25 (not_25_out, j_k_ff_1_qn);
  not not_26 (not_26_out, j_k_ff_3_qn);
  not not_27 (not_27_out, j_k_ff_2_qn);
  not not_28 (not_28_out, j_k_ff_1_qn);
  not not_29 (not_29_out, j_k_ff_2_qn);
  not not_30 (not_30_out, j_k_ff_3_qn);
  not not_31 (not_31_out, j_k_ff_1_qn);
  not not_32 (not_32_out, j_k_ff_1_qn);
  not not_33 (not_33_out, j_k_ff_2_qn);
  not not_34 (not_34_out, j_k_ff_1_qn);
  not not_35 (not_35_out, j_k_ff_4_qn);
  not not_36 (not_36_out, j_k_ff_2_qn);
  not not_37 (not_37_out, j_k_ff_1_qn);
  not not_38 (not_38_out, j_k_ff_3_qn);
  not not_39 (not_39_out, j_k_ff_3_qn);
  not not_40 (not_40_out, j_k_ff_1_qn);
  not not_41 (not_41_out, j_k_ff_4_qn);
  not not_42 (not_42_out, j_k_ff_2_qn);
  not not_43 (not_43_out, j_k_ff_3_qn);
  and and_1 (and_1_out, not_1_out, not_2_out);
  and and_2 (and_2_out, not_3_out, j_k_ff_2_qn);
  and and_3 (and_3_out, not_4_out, j_k_ff_3_qn, j_k_ff_1_qn);
  and and_4 (and_4_out, j_k_ff_3_qn, j_k_ff_2_qn);
  and and_5 (and_5_out, j_k_ff_4_qn, not_5_out, not_6_out);
  and and_6 (and_6_out, j_k_ff_4_qn, not_7_out);
  and and_7 (and_7_out, not_8_out, not_9_out);
  and and_8 (and_8_out, not_10_out, not_11_out, not_12_out);
  and and_9 (and_9_out, not_13_out, not_14_out);
  and and_10 (and_10_out, not_15_out, j_k_ff_2_qn, j_k_ff_1_qn);
  and and_11 (and_11_out, j_k_ff_4_qn, not_16_out, j_k_ff_1_qn);
  and and_12 (and_12_out, not_17_out, not_18_out);
  and and_13 (and_13_out, not_19_out, j_k_ff_1_qn);
  and and_14 (and_14_out, not_20_out, j_k_ff_1_qn);
  and and_15 (and_15_out, not_21_out, j_k_ff_3_qn);
  and and_16 (and_16_out, j_k_ff_4_qn, not_22_out);
  and and_17 (and_17_out, not_23_out, not_24_out, not_25_out);
  and and_18 (and_18_out, not_26_out, j_k_ff_2_qn, j_k_ff_1_qn);
  and and_19 (and_19_out, j_k_ff_3_qn, not_27_out, j_k_ff_1_qn);
  and and_20 (and_20_out, j_k_ff_3_qn, j_k_ff_2_qn, not_28_out);
  and and_21 (and_21_out, j_k_ff_4_qn, not_29_out);
  and and_22 (and_22_out, not_30_out, not_31_out);
  and and_23 (and_23_out, j_k_ff_2_qn, not_32_out);
  and and_24 (and_24_out, j_k_ff_4_qn, j_k_ff_2_qn);
  and and_25 (and_25_out, j_k_ff_4_qn, j_k_ff_3_qn);
  and and_26 (and_26_out, not_33_out, not_34_out);
  and and_27 (and_27_out, not_35_out, j_k_ff_3_qn, not_36_out);
  and and_28 (and_28_out, j_k_ff_3_qn, not_37_out);
  and and_29 (and_29_out, j_k_ff_4_qn, not_38_out);
  and and_30 (and_30_out, j_k_ff_4_qn, j_k_ff_2_qn);
  and and_31 (and_31_out, not_39_out, j_k_ff_2_qn);
  and and_32 (and_32_out, j_k_ff_2_qn, not_40_out);
  and and_33 (and_33_out, not_41_out, j_k_ff_3_qn, not_42_out);
  and and_34 (and_34_out, j_k_ff_4_qn, not_43_out);
  and and_35 (and_35_out, j_k_ff_4_qn, j_k_ff_1_qn);
  or or_1 (a, and_1_out, and_2_out, and_3_out, and_4_out, and_5_out, and_6_out);
  or or_2 (b, and_7_out, and_8_out, and_9_out, and_10_out, and_11_out);
  or or_3 (c, and_12_out, and_13_out, and_14_out, and_15_out, and_16_out);
  or or_4 (d, and_17_out, and_18_out, and_19_out, and_20_out, and_21_out);
  or or_5 (e, and_22_out, and_23_out, and_24_out, and_25_out);
  or or_6 (f, and_26_out, and_27_out, and_28_out, and_29_out, and_30_out);
  or or_7 (g, and_31_out, and_32_out, and_33_out, and_34_out, and_35_out);
  _7_Segment_Display u_7_segment_display_1 (.g(g), .f(f), .a(a), .b(b), .e(e), .d(d), .c(c));  // open: dp
endmodule
